// Logisim project Tetris.circ as structural Verilog: 57 circuits, main circuit main
module main (
);

  wire ButtonLeft, ButtonRight, Clock, comp2_1_out_3, GameReset, led_connector_1_out_2,
       led_connector_1_out_3, led_connector_1_out_4, led_connector_1_out_5, led_connector_1_out_6,
       led_connector_1_out_7, led_connector_1_out_8, led_connector_1_out_9, led_connector_2_out_2,
       led_connector_2_out_3, led_connector_2_out_4, led_connector_2_out_5, led_connector_2_out_6,
       led_connector_2_out_7, led_connector_2_out_8, led_connector_2_out_9, led_connector_3_out_2,
       led_connector_3_out_3, led_connector_3_out_4, led_connector_3_out_5, led_connector_3_out_6,
       led_connector_3_out_7, led_connector_3_out_8, led_connector_3_out_9, led_connector_4_out_2,
       led_connector_4_out_3, led_connector_4_out_4, led_connector_4_out_5, led_connector_4_out_6,
       led_connector_4_out_7, led_connector_4_out_8, led_connector_4_out_9, led_connector_5_out_2,
       led_connector_5_out_3, led_connector_5_out_4, led_connector_5_out_5, led_connector_5_out_6,
       led_connector_5_out_7, led_connector_5_out_8, led_connector_5_out_9, led_connector_6_out_2,
       led_connector_6_out_3, led_connector_6_out_4, led_connector_6_out_5, led_connector_6_out_6,
       led_connector_6_out_7, led_connector_6_out_8, led_connector_6_out_9, led_connector_7_out_2,
       led_connector_7_out_3, led_connector_7_out_4, led_connector_7_out_5, led_connector_7_out_6,
       led_connector_7_out_7, led_connector_7_out_8, led_connector_7_out_9, led_connector_8_out_2,
       led_connector_8_out_3, led_connector_8_out_4, led_connector_8_out_5, led_connector_8_out_6,
       led_connector_8_out_7, led_connector_8_out_8, led_connector_8_out_9, led_connector_9_out_2,
       led_connector_9_out_3, led_connector_9_out_4, led_connector_9_out_5, led_connector_9_out_6,
       led_connector_9_out_7, led_connector_9_out_8, led_connector_9_out_9, led_connector_10_out_2,
       led_connector_10_out_3, led_connector_10_out_4, led_connector_10_out_5, led_connector_10_out_6,
       led_connector_10_out_7, led_connector_10_out_8, led_connector_10_out_9, led_connector_11_out_2,
       led_connector_11_out_3, led_connector_11_out_4, led_connector_11_out_5, led_connector_11_out_6,
       led_connector_11_out_7, led_connector_11_out_8, led_connector_11_out_9, led_connector_12_out_2,
       led_connector_12_out_3, led_connector_12_out_4, led_connector_12_out_5, led_connector_12_out_6,
       led_connector_12_out_7, led_connector_12_out_8, led_connector_12_out_9, not_1_out, or_1_out,
       PlayerReset, scorepointstate_1_line_blink, scorepointstate_1_line_shift, WriteEnable;
  wire [1:0] blockwritestate_1_next_state, CurrentState, gameoverstate_1_next_state, mux4x2_1_out_6,
       player_fsm_1_next_state2, scorepointstate_1_next_state;
  wire [3:0] blockwritestate_1_read_addr, line, player_fsm_1_read_line, raddr, waddr;
  wire [7:0] displaydriver_1_out_8, displaydriver_1_out_9, displaydriver_1_out_10, displaydriver_1_out_11,
       displaydriver_1_out_12, displaydriver_1_out_13, displaydriver_1_out_14, displaydriver_1_out_15,
       displaydriver_1_out_16, displaydriver_1_out_17, displaydriver_1_out_18, displaydriver_1_out_19,
       gameoverstate_1_out_19, gameoverstate_1_out_20, gameoverstate_1_out_21, gameoverstate_1_out_22,
       gameoverstate_1_out_23, gameoverstate_1_out_24, gameoverstate_1_out_25, gameoverstate_1_out_26,
       gameoverstate_1_out_27, gameoverstate_1_out_28, gameoverstate_1_out_29, gameoverstate_1_out_30,
       mask8bit_1_out_3, player, rdata, score, wdata;

  Clock clock_1 (.out(Clock));
  Button button_1 (.out(ButtonLeft));
  // Probe on CurrentState
  // Probe on score
  // Probe on player
  // Probe on line
  Button button_2 (.out(ButtonRight));
  or or_1 (or_1_out, GameReset, PlayerReset);
  DisplayDriver displaydriver_1 (
    .in_1(wdata), .in_2(waddr), .in_3(raddr), .line_shift(scorepointstate_1_line_shift), .Clock(Clock),
    .in_6(WriteEnable), .Reset(GameReset), .out_8(displaydriver_1_out_8), .out_9(displaydriver_1_out_9),
    .out_10(displaydriver_1_out_10), .out_11(displaydriver_1_out_11), .out_12(displaydriver_1_out_12),
    .out_13(displaydriver_1_out_13), .out_14(displaydriver_1_out_14), .out_15(displaydriver_1_out_15),
    .out_16(displaydriver_1_out_16), .out_17(displaydriver_1_out_17), .out_18(displaydriver_1_out_18),
    .out_19(displaydriver_1_out_19), .read_line_data(rdata));
  Mask8bit mask8bit_1 (.in_1(displaydriver_1_out_19), .in_2(not_1_out), .out_3(mask8bit_1_out_3));
  not not_1 (not_1_out, scorepointstate_1_line_blink);
  player_fsm player_fsm_1 (
    .right_button(ButtonRight), .left_button(ButtonLeft), .nb_side(4'b0001), .data_line(rdata),
    .current_state2(CurrentState), .reset(or_1_out), .clock(Clock), .player(player),
    .read_line(player_fsm_1_read_line), .player_line(line), .next_state2(player_fsm_1_next_state2));
  BlockWriteState blockwritestate_1 (
    .current_state(CurrentState), .clock(Clock), .read_line(rdata), .line_number(line), .Player(player),
    .next_state(blockwritestate_1_next_state), .WriteEnable(WriteEnable), .write_addr(waddr),
    .read_addr(blockwritestate_1_read_addr), .write_data(wdata));
  ScorePointState scorepointstate_1 (
    .current_state(CurrentState), .next_state(scorepointstate_1_next_state),
    .line_blink(scorepointstate_1_line_blink), .line_shift(scorepointstate_1_line_shift), .clock(Clock),
    .ScoreReset(GameReset), .Score(score));
  GameOverState gameoverstate_1 (
    .current_state(CurrentState), .Button1(ButtonLeft), .Button2(ButtonRight), .in_4(score),
    .in_5(displaydriver_1_out_8), .in_6(displaydriver_1_out_9), .in_7(displaydriver_1_out_10),
    .in_8(displaydriver_1_out_11), .in_9(displaydriver_1_out_12), .in_10(displaydriver_1_out_13),
    .in_11(displaydriver_1_out_14), .in_12(displaydriver_1_out_15), .in_13(displaydriver_1_out_16),
    .in_14(displaydriver_1_out_17), .in_15(displaydriver_1_out_18), .in_16(mask8bit_1_out_3),
    .next_state(gameoverstate_1_next_state), .GameReset(GameReset), .out_19(gameoverstate_1_out_19),
    .out_20(gameoverstate_1_out_20), .out_21(gameoverstate_1_out_21), .out_22(gameoverstate_1_out_22),
    .out_23(gameoverstate_1_out_23), .out_24(gameoverstate_1_out_24), .out_25(gameoverstate_1_out_25),
    .out_26(gameoverstate_1_out_26), .out_27(gameoverstate_1_out_27), .out_28(gameoverstate_1_out_28),
    .out_29(gameoverstate_1_out_29), .out_30(gameoverstate_1_out_30));
  MUX4x2 mux4x2_1 (
    .in_1(player_fsm_1_next_state2), .in_2(blockwritestate_1_next_state),
    .in_3(scorepointstate_1_next_state), .in_4(gameoverstate_1_next_state), .in_5(CurrentState),
    .out_6(mux4x2_1_out_6));
  Register #(.width(2)) register_1 (.D(mux4x2_1_out_6), .en(1'b1), .clk(Clock), .Q(CurrentState), .clr(1'b0));
  // Probe on mux4x2_1_out_6
  Comp2 comp2_1 (.in_1(CurrentState), .in_2(2'b01), .out_3(comp2_1_out_3));
  LED_Connector led_connector_1 (
    .in_1(gameoverstate_1_out_19), .out_2(led_connector_1_out_2), .out_3(led_connector_1_out_3),
    .out_4(led_connector_1_out_4), .out_5(led_connector_1_out_5), .out_6(led_connector_1_out_6),
    .out_7(led_connector_1_out_7), .out_8(led_connector_1_out_8), .out_9(led_connector_1_out_9));
  LED L50 (.in(led_connector_1_out_4));
  LED L70 (.in(led_connector_1_out_2));
  LED L60 (.in(led_connector_1_out_3));
  LED L61 (.in(led_connector_2_out_3));
  LED L71 (.in(led_connector_2_out_2));
  LED_Connector led_connector_2 (
    .in_1(gameoverstate_1_out_20), .out_2(led_connector_2_out_2), .out_3(led_connector_2_out_3),
    .out_4(led_connector_2_out_4), .out_5(led_connector_2_out_5), .out_6(led_connector_2_out_6),
    .out_7(led_connector_2_out_7), .out_8(led_connector_2_out_8), .out_9(led_connector_2_out_9));
  LED L51 (.in(led_connector_2_out_4));
  LED L62 (.in(led_connector_3_out_3));
  LED L72 (.in(led_connector_3_out_2));
  LED L52 (.in(led_connector_3_out_4));
  LED_Connector led_connector_3 (
    .in_1(gameoverstate_1_out_21), .out_2(led_connector_3_out_2), .out_3(led_connector_3_out_3),
    .out_4(led_connector_3_out_4), .out_5(led_connector_3_out_5), .out_6(led_connector_3_out_6),
    .out_7(led_connector_3_out_7), .out_8(led_connector_3_out_8), .out_9(led_connector_3_out_9));
  LED_Connector led_connector_4 (
    .in_1(gameoverstate_1_out_22), .out_2(led_connector_4_out_2), .out_3(led_connector_4_out_3),
    .out_4(led_connector_4_out_4), .out_5(led_connector_4_out_5), .out_6(led_connector_4_out_6),
    .out_7(led_connector_4_out_7), .out_8(led_connector_4_out_8), .out_9(led_connector_4_out_9));
  LED L63 (.in(led_connector_4_out_3));
  LED L73 (.in(led_connector_4_out_2));
  LED L53 (.in(led_connector_4_out_4));
  LED L54 (.in(led_connector_5_out_4));
  LED L64 (.in(led_connector_5_out_3));
  LED L74 (.in(led_connector_5_out_2));
  LED_Connector led_connector_5 (
    .in_1(gameoverstate_1_out_23), .out_2(led_connector_5_out_2), .out_3(led_connector_5_out_3),
    .out_4(led_connector_5_out_4), .out_5(led_connector_5_out_5), .out_6(led_connector_5_out_6),
    .out_7(led_connector_5_out_7), .out_8(led_connector_5_out_8), .out_9(led_connector_5_out_9));
  LED_Connector led_connector_6 (
    .in_1(gameoverstate_1_out_24), .out_2(led_connector_6_out_2), .out_3(led_connector_6_out_3),
    .out_4(led_connector_6_out_4), .out_5(led_connector_6_out_5), .out_6(led_connector_6_out_6),
    .out_7(led_connector_6_out_7), .out_8(led_connector_6_out_8), .out_9(led_connector_6_out_9));
  LED L55 (.in(led_connector_6_out_4));
  LED L65 (.in(led_connector_6_out_3));
  LED L75 (.in(led_connector_6_out_2));
  LED L66 (.in(led_connector_7_out_3));
  LED L56 (.in(led_connector_7_out_4));
  LED L76 (.in(led_connector_7_out_2));
  LED_Connector led_connector_7 (
    .in_1(gameoverstate_1_out_25), .out_2(led_connector_7_out_2), .out_3(led_connector_7_out_3),
    .out_4(led_connector_7_out_4), .out_5(led_connector_7_out_5), .out_6(led_connector_7_out_6),
    .out_7(led_connector_7_out_7), .out_8(led_connector_7_out_8), .out_9(led_connector_7_out_9));
  LED L57 (.in(led_connector_8_out_4));
  LED L77 (.in(led_connector_8_out_2));
  LED L67 (.in(led_connector_8_out_3));
  LED_Connector led_connector_8 (
    .in_1(gameoverstate_1_out_26), .out_2(led_connector_8_out_2), .out_3(led_connector_8_out_3),
    .out_4(led_connector_8_out_4), .out_5(led_connector_8_out_5), .out_6(led_connector_8_out_6),
    .out_7(led_connector_8_out_7), .out_8(led_connector_8_out_8), .out_9(led_connector_8_out_9));
  LED L58 (.in(led_connector_9_out_4));
  LED_Connector led_connector_9 (
    .in_1(gameoverstate_1_out_27), .out_2(led_connector_9_out_2), .out_3(led_connector_9_out_3),
    .out_4(led_connector_9_out_4), .out_5(led_connector_9_out_5), .out_6(led_connector_9_out_6),
    .out_7(led_connector_9_out_7), .out_8(led_connector_9_out_8), .out_9(led_connector_9_out_9));
  LED L68 (.in(led_connector_9_out_3));
  LED L78 (.in(led_connector_9_out_2));
  LED L79 (.in(led_connector_10_out_2));
  LED_Connector led_connector_10 (
    .in_1(gameoverstate_1_out_28), .out_2(led_connector_10_out_2), .out_3(led_connector_10_out_3),
    .out_4(led_connector_10_out_4), .out_5(led_connector_10_out_5), .out_6(led_connector_10_out_6),
    .out_7(led_connector_10_out_7), .out_8(led_connector_10_out_8), .out_9(led_connector_10_out_9));
  LED L69 (.in(led_connector_10_out_3));
  LED L59 (.in(led_connector_10_out_4));
  LED L5A (.in(led_connector_11_out_4));
  LED L6A (.in(led_connector_11_out_3));
  LED_Connector led_connector_11 (
    .in_1(gameoverstate_1_out_29), .out_2(led_connector_11_out_2), .out_3(led_connector_11_out_3),
    .out_4(led_connector_11_out_4), .out_5(led_connector_11_out_5), .out_6(led_connector_11_out_6),
    .out_7(led_connector_11_out_7), .out_8(led_connector_11_out_8), .out_9(led_connector_11_out_9));
  LED L7A (.in(led_connector_11_out_2));
  LED L5B (.in(led_connector_12_out_4));
  LED_Connector led_connector_12 (
    .in_1(gameoverstate_1_out_30), .out_2(led_connector_12_out_2), .out_3(led_connector_12_out_3),
    .out_4(led_connector_12_out_4), .out_5(led_connector_12_out_5), .out_6(led_connector_12_out_6),
    .out_7(led_connector_12_out_7), .out_8(led_connector_12_out_8), .out_9(led_connector_12_out_9));
  LED L7B (.in(led_connector_12_out_2));
  LED L6B (.in(led_connector_12_out_3));
  MUX2x4 mux2x4_1 (
    .in_1(player_fsm_1_read_line), .in_2(blockwritestate_1_read_addr), .in_3(comp2_1_out_3), .out_4(raddr));
  LED L10 (.in(led_connector_1_out_8));
  LED L20 (.in(led_connector_1_out_7));
  LED L40 (.in(led_connector_1_out_5));
  LED L30 (.in(led_connector_1_out_6));
  LED L21 (.in(led_connector_2_out_7));
  LED L41 (.in(led_connector_2_out_5));
  LED L31 (.in(led_connector_2_out_6));
  LED L11 (.in(led_connector_2_out_8));
  LED L12 (.in(led_connector_3_out_8));
  LED L22 (.in(led_connector_3_out_7));
  LED L32 (.in(led_connector_3_out_6));
  LED L42 (.in(led_connector_3_out_5));
  LED L23 (.in(led_connector_4_out_7));
  LED L33 (.in(led_connector_4_out_6));
  LED L43 (.in(led_connector_4_out_5));
  LED L13 (.in(led_connector_4_out_8));
  LED L14 (.in(led_connector_5_out_8));
  LED L34 (.in(led_connector_5_out_6));
  LED L24 (.in(led_connector_5_out_7));
  LED L44 (.in(led_connector_5_out_5));
  LED L45 (.in(led_connector_6_out_5));
  LED L15 (.in(led_connector_6_out_8));
  LED L25 (.in(led_connector_6_out_7));
  LED L35 (.in(led_connector_6_out_6));
  LED L36 (.in(led_connector_7_out_6));
  LED L16 (.in(led_connector_7_out_8));
  LED L46 (.in(led_connector_7_out_5));
  LED L26 (.in(led_connector_7_out_7));
  LED L17 (.in(led_connector_8_out_8));
  LED L37 (.in(led_connector_8_out_6));
  LED L27 (.in(led_connector_8_out_7));
  LED L47 (.in(led_connector_8_out_5));
  LED L18 (.in(led_connector_9_out_8));
  LED L48 (.in(led_connector_9_out_5));
  LED L28 (.in(led_connector_9_out_7));
  LED L38 (.in(led_connector_9_out_6));
  LED L19 (.in(led_connector_10_out_8));
  LED L39 (.in(led_connector_10_out_6));
  LED L29 (.in(led_connector_10_out_7));
  LED L49 (.in(led_connector_10_out_5));
  LED L4A (.in(led_connector_11_out_5));
  LED L2A (.in(led_connector_11_out_7));
  LED L1A (.in(led_connector_11_out_8));
  LED L3A (.in(led_connector_11_out_6));
  LED L3B (.in(led_connector_12_out_6));
  LED L1B (.in(led_connector_12_out_8));
  LED L2B (.in(led_connector_12_out_7));
  LED L4B (.in(led_connector_12_out_5));
  LED L00 (.in(led_connector_1_out_9));
  LED L01 (.in(led_connector_2_out_9));
  LED L02 (.in(led_connector_3_out_9));
  LED L03 (.in(led_connector_4_out_9));
  LED L04 (.in(led_connector_5_out_9));
  LED L05 (.in(led_connector_6_out_9));
  LED L06 (.in(led_connector_7_out_9));
  LED L07 (.in(led_connector_8_out_9));
  LED L08 (.in(led_connector_9_out_9));
  LED L09 (.in(led_connector_10_out_9));
  LED L0A (.in(led_connector_11_out_9));
  LED L0B (.in(led_connector_12_out_9));
  D_Flip_Flop d_ff_1 (.D(WriteEnable), .clk(Clock), .Q(PlayerReset), .reset(GameReset));  // open: Qn, preset
endmodule

module ledmatrix (
);

  wire led_connector_1_out_2, led_connector_1_out_3, led_connector_1_out_4, led_connector_1_out_5,
       led_connector_1_out_6, led_connector_1_out_7, led_connector_1_out_8, led_connector_1_out_9,
       led_connector_2_out_2, led_connector_2_out_3, led_connector_2_out_4, led_connector_2_out_5,
       led_connector_2_out_6, led_connector_2_out_7, led_connector_2_out_8, led_connector_2_out_9,
       led_connector_3_out_2, led_connector_3_out_3, led_connector_3_out_4, led_connector_3_out_5,
       led_connector_3_out_6, led_connector_3_out_7, led_connector_3_out_8, led_connector_3_out_9,
       led_connector_4_out_2, led_connector_4_out_3, led_connector_4_out_4, led_connector_4_out_5,
       led_connector_4_out_6, led_connector_4_out_7, led_connector_4_out_8, led_connector_4_out_9,
       led_connector_5_out_2, led_connector_5_out_3, led_connector_5_out_4, led_connector_5_out_5,
       led_connector_5_out_6, led_connector_5_out_7, led_connector_5_out_8, led_connector_5_out_9,
       led_connector_6_out_2, led_connector_6_out_3, led_connector_6_out_4, led_connector_6_out_5,
       led_connector_6_out_6, led_connector_6_out_7, led_connector_6_out_8, led_connector_6_out_9,
       led_connector_7_out_2, led_connector_7_out_3, led_connector_7_out_4, led_connector_7_out_5,
       led_connector_7_out_6, led_connector_7_out_7, led_connector_7_out_8, led_connector_7_out_9,
       led_connector_8_out_2, led_connector_8_out_3, led_connector_8_out_4, led_connector_8_out_5,
       led_connector_8_out_6, led_connector_8_out_7, led_connector_8_out_8, led_connector_8_out_9,
       led_connector_9_out_2, led_connector_9_out_3, led_connector_9_out_4, led_connector_9_out_5,
       led_connector_9_out_6, led_connector_9_out_7, led_connector_9_out_8, led_connector_9_out_9,
       led_connector_10_out_2, led_connector_10_out_3, led_connector_10_out_4, led_connector_10_out_5,
       led_connector_10_out_6, led_connector_10_out_7, led_connector_10_out_8, led_connector_10_out_9,
       led_connector_11_out_2, led_connector_11_out_3, led_connector_11_out_4, led_connector_11_out_5,
       led_connector_11_out_6, led_connector_11_out_7, led_connector_11_out_8, led_connector_11_out_9,
       led_connector_12_out_2, led_connector_12_out_3, led_connector_12_out_4, led_connector_12_out_5,
       led_connector_12_out_6, led_connector_12_out_7, led_connector_12_out_8, led_connector_12_out_9;

  LED_Connector led_connector_1 (
    .out_2(led_connector_1_out_2), .out_3(led_connector_1_out_3), .out_4(led_connector_1_out_4),
    .out_5(led_connector_1_out_5), .out_6(led_connector_1_out_6), .out_7(led_connector_1_out_7),
    .out_8(led_connector_1_out_8), .out_9(led_connector_1_out_9));  // open: in_1
  LED L60 (.in(led_connector_1_out_3));
  LED L70 (.in(led_connector_1_out_2));
  LED L71 (.in(led_connector_2_out_2));
  LED L61 (.in(led_connector_2_out_3));
  LED_Connector led_connector_2 (
    .out_2(led_connector_2_out_2), .out_3(led_connector_2_out_3), .out_4(led_connector_2_out_4),
    .out_5(led_connector_2_out_5), .out_6(led_connector_2_out_6), .out_7(led_connector_2_out_7),
    .out_8(led_connector_2_out_8), .out_9(led_connector_2_out_9));  // open: in_1
  LED_Connector led_connector_3 (
    .out_2(led_connector_3_out_2), .out_3(led_connector_3_out_3), .out_4(led_connector_3_out_4),
    .out_5(led_connector_3_out_5), .out_6(led_connector_3_out_6), .out_7(led_connector_3_out_7),
    .out_8(led_connector_3_out_8), .out_9(led_connector_3_out_9));  // open: in_1
  LED L72 (.in(led_connector_3_out_2));
  LED L62 (.in(led_connector_3_out_3));
  LED_Connector led_connector_4 (
    .out_2(led_connector_4_out_2), .out_3(led_connector_4_out_3), .out_4(led_connector_4_out_4),
    .out_5(led_connector_4_out_5), .out_6(led_connector_4_out_6), .out_7(led_connector_4_out_7),
    .out_8(led_connector_4_out_8), .out_9(led_connector_4_out_9));  // open: in_1
  LED L63 (.in(led_connector_4_out_3));
  LED L73 (.in(led_connector_4_out_2));
  LED L64 (.in(led_connector_5_out_3));
  LED_Connector led_connector_5 (
    .out_2(led_connector_5_out_2), .out_3(led_connector_5_out_3), .out_4(led_connector_5_out_4),
    .out_5(led_connector_5_out_5), .out_6(led_connector_5_out_6), .out_7(led_connector_5_out_7),
    .out_8(led_connector_5_out_8), .out_9(led_connector_5_out_9));  // open: in_1
  LED L74 (.in(led_connector_5_out_2));
  LED_Connector led_connector_6 (
    .out_2(led_connector_6_out_2), .out_3(led_connector_6_out_3), .out_4(led_connector_6_out_4),
    .out_5(led_connector_6_out_5), .out_6(led_connector_6_out_6), .out_7(led_connector_6_out_7),
    .out_8(led_connector_6_out_8), .out_9(led_connector_6_out_9));  // open: in_1
  LED L65 (.in(led_connector_6_out_3));
  LED L75 (.in(led_connector_6_out_2));
  LED_Connector led_connector_7 (
    .out_2(led_connector_7_out_2), .out_3(led_connector_7_out_3), .out_4(led_connector_7_out_4),
    .out_5(led_connector_7_out_5), .out_6(led_connector_7_out_6), .out_7(led_connector_7_out_7),
    .out_8(led_connector_7_out_8), .out_9(led_connector_7_out_9));  // open: in_1
  LED L76 (.in(led_connector_7_out_2));
  LED L66 (.in(led_connector_7_out_3));
  LED L77 (.in(led_connector_8_out_2));
  LED_Connector led_connector_8 (
    .out_2(led_connector_8_out_2), .out_3(led_connector_8_out_3), .out_4(led_connector_8_out_4),
    .out_5(led_connector_8_out_5), .out_6(led_connector_8_out_6), .out_7(led_connector_8_out_7),
    .out_8(led_connector_8_out_8), .out_9(led_connector_8_out_9));  // open: in_1
  LED L67 (.in(led_connector_8_out_3));
  LED L78 (.in(led_connector_9_out_2));
  LED_Connector led_connector_9 (
    .out_2(led_connector_9_out_2), .out_3(led_connector_9_out_3), .out_4(led_connector_9_out_4),
    .out_5(led_connector_9_out_5), .out_6(led_connector_9_out_6), .out_7(led_connector_9_out_7),
    .out_8(led_connector_9_out_8), .out_9(led_connector_9_out_9));  // open: in_1
  LED L68 (.in(led_connector_9_out_3));
  LED L69 (.in(led_connector_10_out_3));
  LED L79 (.in(led_connector_10_out_2));
  LED_Connector led_connector_10 (
    .out_2(led_connector_10_out_2), .out_3(led_connector_10_out_3), .out_4(led_connector_10_out_4),
    .out_5(led_connector_10_out_5), .out_6(led_connector_10_out_6), .out_7(led_connector_10_out_7),
    .out_8(led_connector_10_out_8), .out_9(led_connector_10_out_9));  // open: in_1
  LED L7A (.in(led_connector_11_out_2));
  LED L6A (.in(led_connector_11_out_3));
  LED_Connector led_connector_11 (
    .out_2(led_connector_11_out_2), .out_3(led_connector_11_out_3), .out_4(led_connector_11_out_4),
    .out_5(led_connector_11_out_5), .out_6(led_connector_11_out_6), .out_7(led_connector_11_out_7),
    .out_8(led_connector_11_out_8), .out_9(led_connector_11_out_9));  // open: in_1
  LED L6B (.in(led_connector_12_out_3));
  LED L7B (.in(led_connector_12_out_2));
  LED_Connector led_connector_12 (
    .out_2(led_connector_12_out_2), .out_3(led_connector_12_out_3), .out_4(led_connector_12_out_4),
    .out_5(led_connector_12_out_5), .out_6(led_connector_12_out_6), .out_7(led_connector_12_out_7),
    .out_8(led_connector_12_out_8), .out_9(led_connector_12_out_9));  // open: in_1
  LED L50 (.in(led_connector_1_out_4));
  LED L20 (.in(led_connector_1_out_7));
  LED L30 (.in(led_connector_1_out_6));
  LED L40 (.in(led_connector_1_out_5));
  LED L41 (.in(led_connector_2_out_5));
  LED L31 (.in(led_connector_2_out_6));
  LED L21 (.in(led_connector_2_out_7));
  LED L51 (.in(led_connector_2_out_4));
  LED L22 (.in(led_connector_3_out_7));
  LED L32 (.in(led_connector_3_out_6));
  LED L52 (.in(led_connector_3_out_4));
  LED L42 (.in(led_connector_3_out_5));
  LED L53 (.in(led_connector_4_out_4));
  LED L33 (.in(led_connector_4_out_6));
  LED L43 (.in(led_connector_4_out_5));
  LED L23 (.in(led_connector_4_out_7));
  LED L34 (.in(led_connector_5_out_6));
  LED L24 (.in(led_connector_5_out_7));
  LED L54 (.in(led_connector_5_out_4));
  LED L44 (.in(led_connector_5_out_5));
  LED L45 (.in(led_connector_6_out_5));
  LED L55 (.in(led_connector_6_out_4));
  LED L35 (.in(led_connector_6_out_6));
  LED L25 (.in(led_connector_6_out_7));
  LED L56 (.in(led_connector_7_out_4));
  LED L26 (.in(led_connector_7_out_7));
  LED L36 (.in(led_connector_7_out_6));
  LED L46 (.in(led_connector_7_out_5));
  LED L47 (.in(led_connector_8_out_5));
  LED L37 (.in(led_connector_8_out_6));
  LED L57 (.in(led_connector_8_out_4));
  LED L27 (.in(led_connector_8_out_7));
  LED L28 (.in(led_connector_9_out_7));
  LED L48 (.in(led_connector_9_out_5));
  LED L38 (.in(led_connector_9_out_6));
  LED L58 (.in(led_connector_9_out_4));
  LED L49 (.in(led_connector_10_out_5));
  LED L29 (.in(led_connector_10_out_7));
  LED L59 (.in(led_connector_10_out_4));
  LED L39 (.in(led_connector_10_out_6));
  LED L2A (.in(led_connector_11_out_7));
  LED L5A (.in(led_connector_11_out_4));
  LED L4A (.in(led_connector_11_out_5));
  LED L3A (.in(led_connector_11_out_6));
  LED L4B (.in(led_connector_12_out_5));
  LED L2B (.in(led_connector_12_out_7));
  LED L5B (.in(led_connector_12_out_4));
  LED L3B (.in(led_connector_12_out_6));
  LED L00 (.in(led_connector_1_out_9));
  LED L10 (.in(led_connector_1_out_8));
  LED L01 (.in(led_connector_2_out_9));
  LED L11 (.in(led_connector_2_out_8));
  LED L12 (.in(led_connector_3_out_8));
  LED L02 (.in(led_connector_3_out_9));
  LED L13 (.in(led_connector_4_out_8));
  LED L03 (.in(led_connector_4_out_9));
  LED L04 (.in(led_connector_5_out_9));
  LED L14 (.in(led_connector_5_out_8));
  LED L05 (.in(led_connector_6_out_9));
  LED L15 (.in(led_connector_6_out_8));
  LED L06 (.in(led_connector_7_out_9));
  LED L16 (.in(led_connector_7_out_8));
  LED L07 (.in(led_connector_8_out_9));
  LED L17 (.in(led_connector_8_out_8));
  LED L18 (.in(led_connector_9_out_8));
  LED L08 (.in(led_connector_9_out_9));
  LED L09 (.in(led_connector_10_out_9));
  LED L19 (.in(led_connector_10_out_8));
  LED L1A (.in(led_connector_11_out_8));
  LED L0A (.in(led_connector_11_out_9));
  LED L1B (.in(led_connector_12_out_8));
  LED L0B (.in(led_connector_12_out_9));
endmodule

module DisplayMemory (
  input  Reset,
  input  Write_enable,
  input  [7:0] Data_in,
  input  Clock,
  input  [7:0] Data_in_2,
  input  [7:0] Data_in_3,
  input  [7:0] Data_in_4,
  input  [7:0] Data_in_5,
  input  [7:0] Data_in_6,
  input  [7:0] Data_in_7,
  input  [7:0] Data_in_8,
  input  [7:0] Data_in_9,
  input  [7:0] Data_in_10,
  input  [7:0] Data_in_11,
  input  [7:0] Data_in_12,
  output [7:0] Data_out,
  output [7:0] Data_out_2,
  output [7:0] Data_out_3,
  output [7:0] Data_out_4,
  output [7:0] Data_out_5,
  output [7:0] Data_out_6,
  output [7:0] Data_out_7,
  output [7:0] Data_out_8,
  output [7:0] Data_out_9,
  output [7:0] Data_out_10,
  output [7:0] Data_out_11,
  output [7:0] Data_out_12
);

  wire [7:0] or_1_out, or_2_out, or_3_out, or_4_out, or_5_out, or_6_out, or_7_out, or_8_out, or_9_out,
       or_10_out, or_11_out, or_12_out;

  Register register_1 (.D(or_1_out), .en(Write_enable), .clk(Clock), .Q(Data_out), .clr(Reset));
  assign or_1_out = Data_out | Data_in;  // OR_Gate or_1, 8 bits wide
  Register register_2 (.D(or_2_out), .en(Write_enable), .clk(Clock), .Q(Data_out_2), .clr(Reset));
  assign or_2_out = Data_out_2 | Data_in_2;  // OR_Gate or_2, 8 bits wide
  Register register_3 (.D(or_3_out), .en(Write_enable), .clk(Clock), .Q(Data_out_3), .clr(Reset));
  assign or_3_out = Data_out_3 | Data_in_3;  // OR_Gate or_3, 8 bits wide
  Register register_4 (.D(or_4_out), .en(Write_enable), .clk(Clock), .Q(Data_out_4), .clr(Reset));
  assign or_4_out = Data_out_4 | Data_in_4;  // OR_Gate or_4, 8 bits wide
  Register register_5 (.D(or_5_out), .en(Write_enable), .clk(Clock), .Q(Data_out_5), .clr(Reset));
  assign or_5_out = Data_out_5 | Data_in_5;  // OR_Gate or_5, 8 bits wide
  Register register_6 (.D(or_6_out), .en(Write_enable), .clk(Clock), .Q(Data_out_6), .clr(Reset));
  assign or_6_out = Data_out_6 | Data_in_6;  // OR_Gate or_6, 8 bits wide
  Register register_7 (.D(or_7_out), .en(Write_enable), .clk(Clock), .Q(Data_out_7), .clr(Reset));
  assign or_7_out = Data_out_7 | Data_in_7;  // OR_Gate or_7, 8 bits wide
  Register register_8 (.D(or_8_out), .en(Write_enable), .clk(Clock), .Q(Data_out_8), .clr(Reset));
  assign or_8_out = Data_out_8 | Data_in_8;  // OR_Gate or_8, 8 bits wide
  Register register_9 (.D(or_9_out), .en(Write_enable), .clk(Clock), .Q(Data_out_9), .clr(Reset));
  assign or_9_out = Data_out_9 | Data_in_9;  // OR_Gate or_9, 8 bits wide
  Register register_10 (.D(or_10_out), .en(Write_enable), .clk(Clock), .Q(Data_out_10), .clr(Reset));
  assign or_10_out = Data_out_10 | Data_in_10;  // OR_Gate or_10, 8 bits wide
  Register register_11 (.D(or_11_out), .en(Write_enable), .clk(Clock), .Q(Data_out_11), .clr(Reset));
  assign or_11_out = Data_out_11 | Data_in_11;  // OR_Gate or_11, 8 bits wide
  Register register_12 (.D(or_12_out), .en(Write_enable), .clk(Clock), .Q(Data_out_12), .clr(Reset));
  assign or_12_out = Data_out_12 | Data_in_12;  // OR_Gate or_12, 8 bits wide
endmodule

module DisplayDriver (
  input  [7:0] in_1,
  input  [3:0] in_2,
  input  [3:0] in_3,
  input  line_shift,
  input  Clock,
  input  in_6,
  input  Reset,
  output [7:0] out_8,
  output [7:0] out_9,
  output [7:0] out_10,
  output [7:0] out_11,
  output [7:0] out_12,
  output [7:0] out_13,
  output [7:0] out_14,
  output [7:0] out_15,
  output [7:0] out_16,
  output [7:0] out_17,
  output [7:0] out_18,
  output [7:0] out_19,
  output [7:0] read_line_data
);

  wire [7:0] blockmemorydriver_1_out_17, blockmemorydriver_1_out_18, blockmemorydriver_1_out_19,
       blockmemorydriver_1_out_20, blockmemorydriver_1_out_21, blockmemorydriver_1_out_22,
       blockmemorydriver_1_out_23, blockmemorydriver_1_out_24, blockmemorydriver_1_out_25,
       blockmemorydriver_1_out_26, blockmemorydriver_1_out_27, blockmemorydriver_1_out_28, dmx12x8_1_out_3,
       dmx12x8_1_out_4, dmx12x8_1_out_5, dmx12x8_1_out_6, dmx12x8_1_out_7, dmx12x8_1_out_8, dmx12x8_1_out_9,
       dmx12x8_1_out_10, dmx12x8_1_out_11, dmx12x8_1_out_12, dmx12x8_1_out_13, dmx12x8_1_out_14,
       dmx12x8_2_out_3, dmx12x8_2_out_4, dmx12x8_2_out_5, dmx12x8_2_out_6, dmx12x8_2_out_7, dmx12x8_2_out_8,
       dmx12x8_2_out_9, dmx12x8_2_out_10, dmx12x8_2_out_11, dmx12x8_2_out_12, dmx12x8_2_out_13,
       dmx12x8_2_out_14;

  DMX12x8 dmx12x8_1 (
    .in_1(in_1), .in_2(in_2), .out_3(dmx12x8_1_out_3), .out_4(dmx12x8_1_out_4), .out_5(dmx12x8_1_out_5),
    .out_6(dmx12x8_1_out_6), .out_7(dmx12x8_1_out_7), .out_8(dmx12x8_1_out_8), .out_9(dmx12x8_1_out_9),
    .out_10(dmx12x8_1_out_10), .out_11(dmx12x8_1_out_11), .out_12(dmx12x8_1_out_12),
    .out_13(dmx12x8_1_out_13), .out_14(dmx12x8_1_out_14));
  BlockMemoryDriver blockmemorydriver_1 (
    .line_shift(line_shift), .write_enable(in_6), .Reset(Reset), .in_1(dmx12x8_1_out_3),
    .in_2(dmx12x8_1_out_4), .in_3(dmx12x8_1_out_5), .in_4(dmx12x8_1_out_6), .in_5(dmx12x8_1_out_7),
    .in_6(dmx12x8_1_out_8), .in_7(dmx12x8_1_out_9), .in_8(dmx12x8_1_out_10), .in_9(dmx12x8_1_out_11),
    .in_10(dmx12x8_1_out_12), .in_11(dmx12x8_1_out_13), .in_12(dmx12x8_1_out_14),
    .out_17(blockmemorydriver_1_out_17), .out_18(blockmemorydriver_1_out_18),
    .out_19(blockmemorydriver_1_out_19), .out_20(blockmemorydriver_1_out_20),
    .out_21(blockmemorydriver_1_out_21), .out_22(blockmemorydriver_1_out_22),
    .out_23(blockmemorydriver_1_out_23), .out_24(blockmemorydriver_1_out_24),
    .out_25(blockmemorydriver_1_out_25), .out_26(blockmemorydriver_1_out_26),
    .out_27(blockmemorydriver_1_out_27), .out_28(blockmemorydriver_1_out_28), .Clock(Clock));
  DMX12x8 dmx12x8_2 (
    .in_1(in_1), .in_2(in_2), .out_3(dmx12x8_2_out_3), .out_4(dmx12x8_2_out_4), .out_5(dmx12x8_2_out_5),
    .out_6(dmx12x8_2_out_6), .out_7(dmx12x8_2_out_7), .out_8(dmx12x8_2_out_8), .out_9(dmx12x8_2_out_9),
    .out_10(dmx12x8_2_out_10), .out_11(dmx12x8_2_out_11), .out_12(dmx12x8_2_out_12),
    .out_13(dmx12x8_2_out_13), .out_14(dmx12x8_2_out_14));
  OR12 or12_1 (
    .in_13(blockmemorydriver_1_out_17), .in_14(blockmemorydriver_1_out_18),
    .in_15(blockmemorydriver_1_out_19), .in_16(blockmemorydriver_1_out_20),
    .in_17(blockmemorydriver_1_out_21), .in_18(blockmemorydriver_1_out_22),
    .in_19(blockmemorydriver_1_out_23), .in_20(blockmemorydriver_1_out_24),
    .in_21(blockmemorydriver_1_out_25), .in_22(blockmemorydriver_1_out_26),
    .in_23(blockmemorydriver_1_out_27), .in_24(blockmemorydriver_1_out_28), .in_1(dmx12x8_2_out_3),
    .in_2(dmx12x8_2_out_4), .in_3(dmx12x8_2_out_5), .in_4(dmx12x8_2_out_6), .in_5(dmx12x8_2_out_7),
    .in_6(dmx12x8_2_out_8), .in_7(dmx12x8_2_out_9), .in_8(dmx12x8_2_out_10), .in_9(dmx12x8_2_out_11),
    .in_10(dmx12x8_2_out_12), .in_11(dmx12x8_2_out_13), .in_12(dmx12x8_2_out_14), .out_25(out_8),
    .out_26(out_9), .out_27(out_10), .out_28(out_11), .out_29(out_12), .out_30(out_13), .out_31(out_14),
    .out_32(out_15), .out_33(out_16), .out_34(out_17), .out_35(out_18), .out_36(out_19));
  MUX12x8 mux12x8_1 (
    .in_1(out_8), .in_2(out_9), .in_3(out_10), .in_4(out_11), .in_5(out_12), .in_6(out_13), .in_7(out_14),
    .in_8(out_15), .in_9(out_16), .in_10(out_17), .in_11(out_18), .in_12(out_19), .in_13(in_3),
    .out_14(read_line_data));

  // Notes on the sheet:
  //   write line data
  //   write line number
  //   read line number
  //   write enable
  //   Display output
endmodule

module BlockMemory (
  input  WE,
  input  CLK,
  input  Reset,
  input  [7:0] in_4,
  input  [7:0] in_5,
  input  [7:0] in_6,
  input  [7:0] in_7,
  input  [7:0] in_8,
  input  [7:0] in_9,
  input  [7:0] in_10,
  input  [7:0] in_11,
  input  [7:0] in_12,
  input  [7:0] in_13,
  input  [7:0] in_14,
  input  [7:0] in_15,
  output [7:0] out_16,
  output [7:0] out_17,
  output [7:0] out_18,
  output [7:0] out_19,
  output [7:0] out_20,
  output [7:0] out_21,
  output [7:0] out_22,
  output [7:0] out_23,
  output [7:0] out_24,
  output [7:0] out_25,
  output [7:0] out_26,
  output [7:0] out_27
);

  Register register_1 (.D(in_4), .en(WE), .clk(CLK), .Q(out_16), .clr(Reset));
  Register register_2 (.D(in_5), .en(WE), .clk(CLK), .Q(out_17), .clr(Reset));
  Register register_3 (.D(in_6), .en(WE), .clk(CLK), .Q(out_18), .clr(Reset));
  Register register_4 (.D(in_7), .en(WE), .clk(CLK), .Q(out_19), .clr(Reset));
  Register register_5 (.D(in_8), .en(WE), .clk(CLK), .Q(out_20), .clr(Reset));
  Register register_6 (.D(in_9), .en(WE), .clk(CLK), .Q(out_21), .clr(Reset));
  Register register_7 (.D(in_10), .en(WE), .clk(CLK), .Q(out_22), .clr(Reset));
  Register register_8 (.D(in_11), .en(WE), .clk(CLK), .Q(out_23), .clr(Reset));
  Register register_9 (.D(in_12), .en(WE), .clk(CLK), .Q(out_24), .clr(Reset));
  Register register_10 (.D(in_13), .en(WE), .clk(CLK), .Q(out_25), .clr(Reset));
  Register register_11 (.D(in_14), .en(WE), .clk(CLK), .Q(out_26), .clr(Reset));
  Register register_12 (.D(in_15), .en(WE), .clk(CLK), .Q(out_27), .clr(Reset));
endmodule

module BlockMemoryDriver (
  input  [7:0] in_1,
  input  [7:0] in_2,
  input  [7:0] in_3,
  input  [7:0] in_4,
  input  [7:0] in_5,
  input  [7:0] in_6,
  input  [7:0] in_7,
  input  [7:0] in_8,
  input  [7:0] in_9,
  input  [7:0] in_10,
  input  [7:0] in_11,
  input  [7:0] in_12,
  input  line_shift,
  input  write_enable,
  input  Reset,
  input  Clock,
  output [7:0] out_17,
  output [7:0] out_18,
  output [7:0] out_19,
  output [7:0] out_20,
  output [7:0] out_21,
  output [7:0] out_22,
  output [7:0] out_23,
  output [7:0] out_24,
  output [7:0] out_25,
  output [7:0] out_26,
  output [7:0] out_27,
  output [7:0] out_28
);

  wire or_1_out;
  wire [7:0] mask12x8_1_out_14, mask12x8_1_out_15, mask12x8_1_out_16, mask12x8_1_out_17, mask12x8_1_out_18,
       mask12x8_1_out_19, mask12x8_1_out_20, mask12x8_1_out_21, mask12x8_1_out_22, mask12x8_1_out_23,
       mask12x8_1_out_24, mask12x8_1_out_25, mask12x8_2_out_14, mask12x8_2_out_15, mask12x8_2_out_16,
       mask12x8_2_out_17, mask12x8_2_out_18, mask12x8_2_out_19, mask12x8_2_out_20, mask12x8_2_out_21,
       mask12x8_2_out_22, mask12x8_2_out_23, mask12x8_2_out_24, or12_1_out_25, or12_1_out_26, or12_1_out_27,
       or12_1_out_28, or12_1_out_29, or12_1_out_30, or12_1_out_31, or12_1_out_32, or12_1_out_33,
       or12_1_out_34, or12_1_out_35, or12_1_out_36, or12_2_out_25, or12_2_out_26, or12_2_out_27,
       or12_2_out_28, or12_2_out_29, or12_2_out_30, or12_2_out_31, or12_2_out_32, or12_2_out_33,
       or12_2_out_34, or12_2_out_35, or12_2_out_36;
  wire [11:0] not_1_out;

  OR12 or12_1 (
    .in_13(in_1), .in_14(in_2), .in_15(in_3), .in_16(in_4), .in_17(in_5), .in_18(in_6), .in_19(in_7),
    .in_20(in_8), .in_21(in_9), .in_22(in_10), .in_23(in_11), .in_24(in_12), .in_1(out_17), .in_2(out_18),
    .in_3(out_19), .in_4(out_20), .in_5(out_21), .in_6(out_22), .in_7(out_23), .in_8(out_24), .in_9(out_25),
    .in_10(out_26), .in_11(out_27), .in_12(out_28), .out_25(or12_1_out_25), .out_26(or12_1_out_26),
    .out_27(or12_1_out_27), .out_28(or12_1_out_28), .out_29(or12_1_out_29), .out_30(or12_1_out_30),
    .out_31(or12_1_out_31), .out_32(or12_1_out_32), .out_33(or12_1_out_33), .out_34(or12_1_out_34),
    .out_35(or12_1_out_35), .out_36(or12_1_out_36));
  or or_1 (or_1_out, line_shift, write_enable);
  Mask12x8 mask12x8_1 (
    .in_1(or12_1_out_25), .in_2(or12_1_out_26), .in_3(or12_1_out_27), .in_4(or12_1_out_28),
    .in_5(or12_1_out_29), .in_6(or12_1_out_30), .in_7(or12_1_out_31), .in_8(or12_1_out_32),
    .in_9(or12_1_out_33), .in_10(or12_1_out_34), .in_11(or12_1_out_35), .in_12(or12_1_out_36),
    .in_13(not_1_out), .out_14(mask12x8_1_out_14), .out_15(mask12x8_1_out_15), .out_16(mask12x8_1_out_16),
    .out_17(mask12x8_1_out_17), .out_18(mask12x8_1_out_18), .out_19(mask12x8_1_out_19),
    .out_20(mask12x8_1_out_20), .out_21(mask12x8_1_out_21), .out_22(mask12x8_1_out_22),
    .out_23(mask12x8_1_out_23), .out_24(mask12x8_1_out_24), .out_25(mask12x8_1_out_25));
  assign not_1_out = ~{12{line_shift}};  // NOT_Gate not_1, 12 bits wide
  Mask12x8 mask12x8_2 (
    .in_1(out_17), .in_2(out_18), .in_3(out_19), .in_4(out_20), .in_5(out_21), .in_6(out_22), .in_7(out_23),
    .in_8(out_24), .in_9(out_25), .in_10(out_26), .in_11(out_27), .in_12(out_28), .in_13({12{line_shift}}),
    .out_14(mask12x8_2_out_14), .out_15(mask12x8_2_out_15), .out_16(mask12x8_2_out_16),
    .out_17(mask12x8_2_out_17), .out_18(mask12x8_2_out_18), .out_19(mask12x8_2_out_19),
    .out_20(mask12x8_2_out_20), .out_21(mask12x8_2_out_21), .out_22(mask12x8_2_out_22),
    .out_23(mask12x8_2_out_23), .out_24(mask12x8_2_out_24));  // open: out_25
  OR12 or12_2 (
    .in_13(mask12x8_1_out_14), .in_14(mask12x8_1_out_15), .in_15(mask12x8_1_out_16),
    .in_16(mask12x8_1_out_17), .in_17(mask12x8_1_out_18), .in_18(mask12x8_1_out_19),
    .in_19(mask12x8_1_out_20), .in_20(mask12x8_1_out_21), .in_21(mask12x8_1_out_22),
    .in_22(mask12x8_1_out_23), .in_23(mask12x8_1_out_24), .in_24(mask12x8_1_out_25), .in_1({8{1'b0}}),
    .in_2(mask12x8_2_out_14), .in_3(mask12x8_2_out_15), .in_4(mask12x8_2_out_16), .in_5(mask12x8_2_out_17),
    .in_6(mask12x8_2_out_18), .in_7(mask12x8_2_out_19), .in_8(mask12x8_2_out_20), .in_9(mask12x8_2_out_21),
    .in_10(mask12x8_2_out_22), .in_11(mask12x8_2_out_23), .in_12(mask12x8_2_out_24), .out_25(or12_2_out_25),
    .out_26(or12_2_out_26), .out_27(or12_2_out_27), .out_28(or12_2_out_28), .out_29(or12_2_out_29),
    .out_30(or12_2_out_30), .out_31(or12_2_out_31), .out_32(or12_2_out_32), .out_33(or12_2_out_33),
    .out_34(or12_2_out_34), .out_35(or12_2_out_35), .out_36(or12_2_out_36));
  BlockMemory blockmemory_1 (
    .WE(or_1_out), .CLK(Clock), .Reset(Reset), .in_4(or12_2_out_25), .in_5(or12_2_out_26),
    .in_6(or12_2_out_27), .in_7(or12_2_out_28), .in_8(or12_2_out_29), .in_9(or12_2_out_30),
    .in_10(or12_2_out_31), .in_11(or12_2_out_32), .in_12(or12_2_out_33), .in_13(or12_2_out_34),
    .in_14(or12_2_out_35), .in_15(or12_2_out_36), .out_16(out_17), .out_17(out_18), .out_18(out_19),
    .out_19(out_20), .out_20(out_21), .out_21(out_22), .out_22(out_23), .out_23(out_24), .out_24(out_25),
    .out_25(out_26), .out_26(out_27), .out_27(out_28));
endmodule

module Comp12bit (
  input  [11:0] in_1,
  input  [11:0] in_2,
  output out_3
);

  wire [11:0] xor_1_out;

  assign xor_1_out = in_1 ^ in_2;  // XOR_Gate xor_1, 12 bits wide
  nor nor_1 (out_3, xor_1_out[0], xor_1_out[1], xor_1_out[2], xor_1_out[3], xor_1_out[4], xor_1_out[5], xor_1_out[6], xor_1_out[7], xor_1_out[8], xor_1_out[9], xor_1_out[10], xor_1_out[11]);
endmodule

module GTEQ12 (
  input  [3:0] in_1,
  output o0,
  output o1,
  output o2,
  output o3,
  output o4,
  output o5,
  output o6,
  output o7,
  output o8,
  output o9,
  output o10,
  output o11
);

  wire and_1_out, and_2_out, and_3_out, and_4_out, and_5_out, and_6_out, and_7_out, and_8_out, and_9_out,
       and_10_out, and_11_out, and_12_out;

  or or_1 (o1, in_1[0], in_1[1], in_1[2], in_1[3]);
  or or_2 (o2, in_1[1], in_1[2], in_1[3]);
  and and_1 (and_1_out, in_1[1], in_1[0]);
  or or_3 (o3, and_1_out, in_1[2], in_1[3]);
  or or_4 (o4, in_1[2], in_1[3]);
  and and_2 (and_2_out, in_1[2], in_1[0]);
  or or_5 (o5, and_2_out, and_3_out, in_1[3]);
  and and_3 (and_3_out, in_1[2], in_1[1]);
  and and_4 (and_4_out, in_1[2], in_1[1]);
  or or_6 (o6, and_4_out, in_1[3]);
  and and_5 (and_5_out, in_1[2], in_1[1], in_1[0]);
  or or_7 (o7, and_5_out, in_1[3]);
  and and_6 (and_6_out, in_1[3], in_1[0]);
  or or_8 (o9, and_6_out, and_7_out, and_8_out);
  and and_7 (and_7_out, in_1[3], in_1[1]);
  and and_8 (and_8_out, in_1[3], in_1[2]);
  and and_9 (and_9_out, in_1[3], in_1[1]);
  or or_9 (o10, and_9_out, and_10_out);
  and and_10 (and_10_out, in_1[3], in_1[2]);
  and and_11 (and_11_out, in_1[3], in_1[1], in_1[0]);
  or or_10 (o11, and_11_out, and_12_out);
  and and_12 (and_12_out, in_1[3], in_1[2]);

  assign o0 = 1'b1;
  assign o8 = in_1[3];
endmodule

module mux12helper (
  input  [3:0] in_1,
  output o0,
  output o1,
  output o2,
  output o3,
  output o4,
  output o5,
  output o6,
  output o7,
  output o8,
  output o9,
  output o10,
  output o11
);

  wire not_1_out, not_2_out, not_3_out, not_4_out, not_5_out, not_6_out, not_7_out, not_8_out, not_9_out,
       not_10_out, not_11_out, not_12_out, not_13_out, not_14_out, not_15_out, not_16_out, not_17_out,
       not_18_out, not_19_out, not_20_out, not_21_out, not_22_out, not_23_out, not_24_out, not_25_out,
       not_26_out, not_27_out, not_28_out;

  not not_1 (not_1_out, in_1[3]);
  not not_2 (not_2_out, in_1[2]);
  not not_3 (not_3_out, in_1[1]);
  not not_4 (not_4_out, in_1[0]);
  not not_5 (not_5_out, in_1[3]);
  not not_6 (not_6_out, in_1[2]);
  not not_7 (not_7_out, in_1[1]);
  not not_8 (not_8_out, in_1[3]);
  not not_9 (not_9_out, in_1[2]);
  not not_10 (not_10_out, in_1[0]);
  not not_11 (not_11_out, in_1[3]);
  not not_12 (not_12_out, in_1[2]);
  not not_13 (not_13_out, in_1[3]);
  not not_14 (not_14_out, in_1[1]);
  not not_15 (not_15_out, in_1[0]);
  not not_16 (not_16_out, in_1[3]);
  not not_17 (not_17_out, in_1[1]);
  not not_18 (not_18_out, in_1[3]);
  not not_19 (not_19_out, in_1[0]);
  not not_20 (not_20_out, in_1[3]);
  not not_21 (not_21_out, in_1[2]);
  not not_22 (not_22_out, in_1[1]);
  not not_23 (not_23_out, in_1[0]);
  not not_24 (not_24_out, in_1[2]);
  not not_25 (not_25_out, in_1[1]);
  not not_26 (not_26_out, in_1[2]);
  not not_27 (not_27_out, in_1[0]);
  not not_28 (not_28_out, in_1[2]);
  and and_1 (o0, not_1_out, not_2_out, not_3_out, not_4_out);
  and and_2 (o1, not_5_out, not_6_out, not_7_out, in_1[0]);
  and and_3 (o2, not_8_out, not_9_out, in_1[1], not_10_out);
  and and_4 (o3, not_11_out, not_12_out, in_1[1], in_1[0]);
  and and_5 (o4, not_13_out, in_1[2], not_14_out, not_15_out);
  and and_6 (o5, not_16_out, in_1[2], not_17_out, in_1[0]);
  and and_7 (o6, not_18_out, in_1[2], in_1[1], not_19_out);
  and and_8 (o7, not_20_out, in_1[2], in_1[1], in_1[0]);
  and and_9 (o8, in_1[3], not_21_out, not_22_out, not_23_out);
  and and_10 (o9, in_1[3], not_24_out, not_25_out, in_1[0]);
  and and_11 (o10, in_1[3], not_26_out, in_1[1], not_27_out);
  and and_12 (o11, in_1[3], not_28_out, in_1[1], in_1[0]);
endmodule

module MUX12x8 (
  input  [7:0] in_1,
  input  [7:0] in_2,
  input  [7:0] in_3,
  input  [7:0] in_4,
  input  [7:0] in_5,
  input  [7:0] in_6,
  input  [7:0] in_7,
  input  [7:0] in_8,
  input  [7:0] in_9,
  input  [7:0] in_10,
  input  [7:0] in_11,
  input  [7:0] in_12,
  input  [3:0] in_13,
  output [7:0] out_14
);

  wire mux12helper_1_o0, mux12helper_1_o1, mux12helper_1_o2, mux12helper_1_o3, mux12helper_1_o4,
       mux12helper_1_o5, mux12helper_1_o6, mux12helper_1_o7, mux12helper_1_o8, mux12helper_1_o9,
       mux12helper_1_o10, mux12helper_1_o11;
  wire [7:0] mask8bit_1_out_3, mask8bit_2_out_3, mask8bit_3_out_3, mask8bit_4_out_3, mask8bit_5_out_3,
       mask8bit_6_out_3, mask8bit_7_out_3, mask8bit_8_out_3, mask8bit_9_out_3, mask8bit_10_out_3,
       mask8bit_11_out_3, mask8bit_12_out_3;

  Mask8bit mask8bit_1 (.in_1(in_1), .in_2(mux12helper_1_o0), .out_3(mask8bit_1_out_3));
  mux12helper mux12helper_1 (
    .in_1(in_13), .o0(mux12helper_1_o0), .o1(mux12helper_1_o1), .o2(mux12helper_1_o2), .o3(mux12helper_1_o3),
    .o4(mux12helper_1_o4), .o5(mux12helper_1_o5), .o6(mux12helper_1_o6), .o7(mux12helper_1_o7),
    .o8(mux12helper_1_o8), .o9(mux12helper_1_o9), .o10(mux12helper_1_o10), .o11(mux12helper_1_o11));
  Mask8bit mask8bit_2 (.in_1(in_2), .in_2(mux12helper_1_o1), .out_3(mask8bit_2_out_3));
  Mask8bit mask8bit_3 (.in_1(in_3), .in_2(mux12helper_1_o2), .out_3(mask8bit_3_out_3));
  Mask8bit mask8bit_4 (.in_1(in_4), .in_2(mux12helper_1_o3), .out_3(mask8bit_4_out_3));
  Mask8bit mask8bit_5 (.in_1(in_5), .in_2(mux12helper_1_o4), .out_3(mask8bit_5_out_3));
  Mask8bit mask8bit_6 (.in_1(in_6), .in_2(mux12helper_1_o5), .out_3(mask8bit_6_out_3));
  Mask8bit mask8bit_7 (.in_1(in_7), .in_2(mux12helper_1_o6), .out_3(mask8bit_7_out_3));
  Mask8bit mask8bit_8 (.in_1(in_8), .in_2(mux12helper_1_o7), .out_3(mask8bit_8_out_3));
  Mask8bit mask8bit_9 (.in_1(in_9), .in_2(mux12helper_1_o8), .out_3(mask8bit_9_out_3));
  Mask8bit mask8bit_10 (.in_1(in_10), .in_2(mux12helper_1_o9), .out_3(mask8bit_10_out_3));
  Mask8bit mask8bit_11 (.in_1(in_11), .in_2(mux12helper_1_o10), .out_3(mask8bit_11_out_3));
  Mask8bit mask8bit_12 (.in_1(in_12), .in_2(mux12helper_1_o11), .out_3(mask8bit_12_out_3));
  assign out_14 = mask8bit_1_out_3 | mask8bit_2_out_3 | mask8bit_3_out_3 | mask8bit_4_out_3 | mask8bit_5_out_3 | mask8bit_6_out_3 | mask8bit_7_out_3 | mask8bit_8_out_3 | mask8bit_9_out_3 | mask8bit_10_out_3 | mask8bit_11_out_3 | mask8bit_12_out_3;  // OR_Gate or_1, 8 bits wide
endmodule

module Mask8bit (
  input  [7:0] in_1,
  input  in_2,
  output [7:0] out_3
);

  assign out_3 = in_1 & {8{in_2}};  // AND_Gate and_1, 8 bits wide
endmodule

module DMX12x8 (
  input  [7:0] in_1,
  input  [3:0] in_2,
  output [7:0] out_3,
  output [7:0] out_4,
  output [7:0] out_5,
  output [7:0] out_6,
  output [7:0] out_7,
  output [7:0] out_8,
  output [7:0] out_9,
  output [7:0] out_10,
  output [7:0] out_11,
  output [7:0] out_12,
  output [7:0] out_13,
  output [7:0] out_14
);

  wire mux12helper_1_o0, mux12helper_1_o1, mux12helper_1_o2, mux12helper_1_o3, mux12helper_1_o4,
       mux12helper_1_o5, mux12helper_1_o6, mux12helper_1_o7, mux12helper_1_o8, mux12helper_1_o9,
       mux12helper_1_o10, mux12helper_1_o11;

  Mask8bit mask8bit_1 (.in_1(in_1), .in_2(mux12helper_1_o0), .out_3(out_3));
  mux12helper mux12helper_1 (
    .in_1(in_2), .o0(mux12helper_1_o0), .o1(mux12helper_1_o1), .o2(mux12helper_1_o2), .o3(mux12helper_1_o3),
    .o4(mux12helper_1_o4), .o5(mux12helper_1_o5), .o6(mux12helper_1_o6), .o7(mux12helper_1_o7),
    .o8(mux12helper_1_o8), .o9(mux12helper_1_o9), .o10(mux12helper_1_o10), .o11(mux12helper_1_o11));
  Mask8bit mask8bit_2 (.in_1(in_1), .in_2(mux12helper_1_o1), .out_3(out_4));
  Mask8bit mask8bit_3 (.in_1(in_1), .in_2(mux12helper_1_o2), .out_3(out_5));
  Mask8bit mask8bit_4 (.in_1(in_1), .in_2(mux12helper_1_o3), .out_3(out_6));
  Mask8bit mask8bit_5 (.in_1(in_1), .in_2(mux12helper_1_o4), .out_3(out_7));
  Mask8bit mask8bit_6 (.in_1(in_1), .in_2(mux12helper_1_o5), .out_3(out_8));
  Mask8bit mask8bit_7 (.in_1(in_1), .in_2(mux12helper_1_o6), .out_3(out_9));
  Mask8bit mask8bit_8 (.in_1(in_1), .in_2(mux12helper_1_o7), .out_3(out_10));
  Mask8bit mask8bit_9 (.in_1(in_1), .in_2(mux12helper_1_o8), .out_3(out_11));
  Mask8bit mask8bit_10 (.in_1(in_1), .in_2(mux12helper_1_o9), .out_3(out_12));
  Mask8bit mask8bit_11 (.in_1(in_1), .in_2(mux12helper_1_o10), .out_3(out_13));
  Mask8bit mask8bit_12 (.in_1(in_1), .in_2(mux12helper_1_o11), .out_3(out_14));
endmodule

module Mask12x8 (
  input  [7:0] in_1,
  input  [7:0] in_2,
  input  [7:0] in_3,
  input  [7:0] in_4,
  input  [7:0] in_5,
  input  [7:0] in_6,
  input  [7:0] in_7,
  input  [7:0] in_8,
  input  [7:0] in_9,
  input  [7:0] in_10,
  input  [7:0] in_11,
  input  [7:0] in_12,
  input  [11:0] in_13,
  output [7:0] out_14,
  output [7:0] out_15,
  output [7:0] out_16,
  output [7:0] out_17,
  output [7:0] out_18,
  output [7:0] out_19,
  output [7:0] out_20,
  output [7:0] out_21,
  output [7:0] out_22,
  output [7:0] out_23,
  output [7:0] out_24,
  output [7:0] out_25
);

  Mask8bit mask8bit_1 (.in_1(in_1), .in_2(in_13[0]), .out_3(out_14));
  Mask8bit mask8bit_2 (.in_1(in_2), .in_2(in_13[1]), .out_3(out_15));
  Mask8bit mask8bit_3 (.in_1(in_3), .in_2(in_13[2]), .out_3(out_16));
  Mask8bit mask8bit_4 (.in_1(in_4), .in_2(in_13[3]), .out_3(out_17));
  Mask8bit mask8bit_5 (.in_1(in_5), .in_2(in_13[4]), .out_3(out_18));
  Mask8bit mask8bit_6 (.in_1(in_6), .in_2(in_13[5]), .out_3(out_19));
  Mask8bit mask8bit_7 (.in_1(in_7), .in_2(in_13[6]), .out_3(out_20));
  Mask8bit mask8bit_8 (.in_1(in_8), .in_2(in_13[7]), .out_3(out_21));
  Mask8bit mask8bit_9 (.in_1(in_9), .in_2(in_13[8]), .out_3(out_22));
  Mask8bit mask8bit_10 (.in_1(in_10), .in_2(in_13[9]), .out_3(out_23));
  Mask8bit mask8bit_11 (.in_1(in_11), .in_2(in_13[10]), .out_3(out_24));
  Mask8bit mask8bit_12 (.in_1(in_12), .in_2(in_13[11]), .out_3(out_25));
endmodule

module OR12 (
  input  [7:0] in_1,
  input  [7:0] in_2,
  input  [7:0] in_3,
  input  [7:0] in_4,
  input  [7:0] in_5,
  input  [7:0] in_6,
  input  [7:0] in_7,
  input  [7:0] in_8,
  input  [7:0] in_9,
  input  [7:0] in_10,
  input  [7:0] in_11,
  input  [7:0] in_12,
  input  [7:0] in_13,
  input  [7:0] in_14,
  input  [7:0] in_15,
  input  [7:0] in_16,
  input  [7:0] in_17,
  input  [7:0] in_18,
  input  [7:0] in_19,
  input  [7:0] in_20,
  input  [7:0] in_21,
  input  [7:0] in_22,
  input  [7:0] in_23,
  input  [7:0] in_24,
  output [7:0] out_25,
  output [7:0] out_26,
  output [7:0] out_27,
  output [7:0] out_28,
  output [7:0] out_29,
  output [7:0] out_30,
  output [7:0] out_31,
  output [7:0] out_32,
  output [7:0] out_33,
  output [7:0] out_34,
  output [7:0] out_35,
  output [7:0] out_36
);

  assign out_25 = in_1 | in_13;  // OR_Gate or_1, 8 bits wide
  assign out_26 = in_2 | in_14;  // OR_Gate or_2, 8 bits wide
  assign out_27 = in_3 | in_15;  // OR_Gate or_3, 8 bits wide
  assign out_28 = in_4 | in_16;  // OR_Gate or_4, 8 bits wide
  assign out_29 = in_5 | in_17;  // OR_Gate or_5, 8 bits wide
  assign out_30 = in_6 | in_18;  // OR_Gate or_6, 8 bits wide
  assign out_31 = in_7 | in_19;  // OR_Gate or_7, 8 bits wide
  assign out_32 = in_8 | in_20;  // OR_Gate or_8, 8 bits wide
  assign out_33 = in_9 | in_21;  // OR_Gate or_9, 8 bits wide
  assign out_34 = in_10 | in_22;  // OR_Gate or_10, 8 bits wide
  assign out_35 = in_11 | in_23;  // OR_Gate or_11, 8 bits wide
  assign out_36 = in_12 | in_24;  // OR_Gate or_12, 8 bits wide
endmodule

module BlockWriteState (
  input  [1:0] current_state,
  input  clock,
  input  [7:0] read_line,
  input  [3:0] line_number,
  input  [7:0] Player,
  output [1:0] next_state,
  output WriteEnable,
  output [3:0] write_addr,
  output [3:0] read_addr,
  output [7:0] write_data
);

  wire active, comp2_2_out_3, comp4_1_out_3, GameOver, LineFull, not_1_out;
  wire [1:0] inc2bit_1_out_2, LocalState, mux2x2_1_out_4, mux2x2_2_out_4;
  wire [7:0] register_2_q, xor_1_out;

  Comp2 comp2_1 (.in_1(current_state), .in_2(2'b01), .out_3(active));
  Register #(.width(2)) register_1 (.D(inc2bit_1_out_2), .en(1'b1), .clk(clock), .Q(LocalState), .clr(not_1_out));
  Inc2bit inc2bit_1 (.in_1(LocalState), .out_2(inc2bit_1_out_2));
  Comp4 comp4_1 (.in_1(4'b0000), .in_2(line_number), .out_3(comp4_1_out_3));
  not not_1 (not_1_out, active);
  Register register_2 (.D(read_line), .en(1'b1), .clk(clock), .Q(register_2_q), .clr(1'b0));
  assign xor_1_out = {8{1'b1}} ^ register_2_q;  // XOR_Gate xor_1, 8 bits wide
  D_Flip_Flop d_ff_1 (.D(comp4_1_out_3), .clk(clock), .Q(GameOver));  // open: Qn, preset, reset
  nor nor_1 (LineFull, xor_1_out[0], xor_1_out[1], xor_1_out[2], xor_1_out[3], xor_1_out[4], xor_1_out[5], xor_1_out[6], xor_1_out[7]);
  MUX2x2 mux2x2_1 (.in_1(2'b00), .in_2(2'b10), .in_3(LineFull), .out_4(mux2x2_1_out_4));
  MUX2x2 mux2x2_2 (.in_1(mux2x2_1_out_4), .in_2(2'b11), .in_3(GameOver), .out_4(mux2x2_2_out_4));
  Comp2 comp2_2 (.in_1(LocalState), .in_2(2'b00), .out_3(comp2_2_out_3));
  and and_1 (WriteEnable, comp2_2_out_3, active);
  MUX4x2 mux4x2_1 (
    .in_1(2'b01), .in_2(mux2x2_2_out_4), .in_3(2'b00), .in_4(2'b00), .in_5(LocalState), .out_6(next_state));

  assign read_addr = line_number;
  assign write_addr = line_number;
  assign write_data = Player;

  // Notes on the sheet:
  //   second phase: read line from memory
  //   local state variable
  //   If first line, then game over
  //   PlayerState
  //   LineDeleteState
  //   third phase: choose next state
  //   first phase: write block to memory
endmodule

module MUX2x2 (
  input  [1:0] in_1,
  input  [1:0] in_2,
  input  in_3,
  output [1:0] out_4
);

  wire [1:0] and_1_out, and_2_out, not_1_out;

  assign not_1_out = ~{2{in_3}};  // NOT_Gate not_1, 2 bits wide
  assign and_1_out = not_1_out & in_1;  // AND_Gate and_1, 2 bits wide
  assign and_2_out = in_2 & {2{in_3}};  // AND_Gate and_2, 2 bits wide
  assign out_4 = and_1_out | and_2_out;  // OR_Gate or_1, 2 bits wide
endmodule

module MUX4x2 (
  input  [1:0] in_1,
  input  [1:0] in_2,
  input  [1:0] in_3,
  input  [1:0] in_4,
  input  [1:0] in_5,
  output [1:0] out_6
);

  wire [1:0] and_1_out, and_2_out, and_3_out, and_4_out;
  wire [1:1] not_1_out, not_2_out, not_3_out, not_4_out;

  not not_1 (not_1_out[1], in_5[0]);
  not not_2 (not_2_out[1], in_5[1]);
  not not_3 (not_3_out[1], in_5[1]);
  not not_4 (not_4_out[1], in_5[0]);
  assign and_1_out = {2{not_1_out[1]}} & in_1 & {2{not_2_out[1]}};  // AND_Gate and_1, 2 bits wide
  assign and_2_out = {2{in_5[0]}} & in_2 & {2{not_3_out[1]}};  // AND_Gate and_2, 2 bits wide
  assign and_3_out = {2{not_4_out[1]}} & in_3 & {2{in_5[1]}};  // AND_Gate and_3, 2 bits wide
  assign and_4_out = {2{in_5[0]}} & in_4 & {2{in_5[1]}};  // AND_Gate and_4, 2 bits wide
  assign out_6 = and_1_out | and_2_out | and_3_out | and_4_out;  // OR_Gate or_1, 2 bits wide
endmodule

module Comp2 (
  input  [1:0] in_1,
  input  [1:0] in_2,
  output out_3
);

  wire [1:0] xor_1_out;

  assign xor_1_out = in_1 ^ in_2;  // XOR_Gate xor_1, 2 bits wide
  nor nor_1 (out_3, xor_1_out[0], xor_1_out[1]);
endmodule

module Inc2bit (
  input  [1:0] in_1,
  output [1:0] out_2
);

  wire half_adder_2_c;

  Half_adder half_adder_1 (.A(in_1[1]), .B(half_adder_2_c), .Q(out_2[1]));  // open: C
  Half_adder half_adder_2 (.A(in_1[0]), .B(1'b1), .Q(out_2[0]), .C(half_adder_2_c));
endmodule

module ScorePointState (
  input  [1:0] current_state,
  input  clock,
  input  ScoreReset,
  output [1:0] next_state,
  output line_blink,
  output line_shift,
  output [7:0] Score
);

  wire active, and_1_out, clockdiv_1_clock_output, comp2_2_out_3, comp3_1_out_3, d_ff_1_q, IncState,
       not_1_out, not_2_out;
  wire [1:0] inc2bit_1_out_2, LocalState, mux2x2_1_out_4;
  wire [2:0] inc3bit_1_out_2, register_2_q;

  Inc2bit inc2bit_1 (.in_1(LocalState), .out_2(inc2bit_1_out_2));
  Pull_Resistor pull_resistor_1 (.node(IncState));
  Comp2 comp2_1 (.in_1(current_state), .in_2(2'b10), .out_3(active));
  Register #(.width(2)) register_1 (.D(mux2x2_1_out_4), .en(1'b1), .clk(clock), .Q(LocalState), .clr(not_1_out));
  // Probe on mux2x2_1_out_4
  MUX2x2 mux2x2_1 (.in_1(LocalState), .in_2(inc2bit_1_out_2), .in_3(IncState), .out_4(mux2x2_1_out_4));
  not not_1 (not_1_out, active);
  Comp2 comp2_2 (.in_1(LocalState), .in_2(2'b00), .out_3(comp2_2_out_3));
  ClockDiv clockdiv_1 (.Clock_input(clock), .N_div_power(2'b01), .Clock_output(clockdiv_1_clock_output));
  and and_1 (and_1_out, comp2_2_out_3, active);
  Register #(.width(3)) register_2 (
    .D(inc3bit_1_out_2), .en(and_1_out), .clk(clockdiv_1_clock_output), .Q(register_2_q), .clr(not_2_out));
  Inc3bit inc3bit_1 (.in_1(register_2_q), .out_2(inc3bit_1_out_2));
  not not_2 (not_2_out, and_1_out);
  Comp2 comp2_3 (.in_1(LocalState), .in_2(2'b01), .out_3(line_shift));
  assign IncState = line_shift ? line_shift : 1'bz;  // Controlled_Buffer controlled_buffer_1
  MUX4x2 mux4x2_1 (.in_1(2'b10), .in_2(2'b10), .in_3(2'b00), .in_5(LocalState), .out_6(next_state));  // open: in_4
  Comp3 comp3_1 (.in_1(register_2_q), .in_2(3'b101), .out_3(comp3_1_out_3));
  ScoreCounter scorecounter_1 (.clock(line_shift), .score_reset(ScoreReset), .out_3(Score));
  D_Flip_Flop d_ff_1 (
    .D(comp3_1_out_3), .clk(clockdiv_1_clock_output), .Q(d_ff_1_q), .reset(not_2_out));  // open: Qn, preset
  and and_2 (line_blink, and_1_out, register_2_q[0]);
  assign IncState = d_ff_1_q ? d_ff_1_q : 1'bz;  // Controlled_Buffer controlled_buffer_2

  // Notes on the sheet:
  //   local state variable
  //   blink
endmodule

module ScoreCounter (
  input  clock,
  input  score_reset,
  output [7:0] out_3
);

  wire comp4_1_out_3;
  wire [3:0] inc4bit_1_out_2, inc4bit_2_out_2, mux2x4_1_out_4;

  Inc4bit inc4bit_1 (.in_1(out_3[3:0]), .out_2(inc4bit_1_out_2));
  Comp4 comp4_1 (.in_1(inc4bit_1_out_2), .in_2(4'b1010), .out_3(comp4_1_out_3));
  MUX2x4 mux2x4_1 (.in_1(4'b0000), .in_2(inc4bit_1_out_2), .in_3(comp4_1_out_3), .out_4(mux2x4_1_out_4));
  Register #(.width(4)) register_1 (.D(mux2x4_1_out_4), .en(1'b1), .clk(clock), .Q(out_3[3:0]), .clr(score_reset));
  Inc4bit inc4bit_2 (.in_1(out_3[7:4]), .out_2(inc4bit_2_out_2));
  Register #(.width(4)) register_2 (
    .D(inc4bit_2_out_2), .en(comp4_1_out_3), .clk(clock), .Q(out_3[7:4]), .clr(score_reset));

  // Notes on the sheet:
  //   score low
  //   score high
endmodule

module Inc8bit (
  input  [7:0] in_1,
  output [7:0] out_2
);

  wire half_adder_2_c, half_adder_3_c, half_adder_4_c, half_adder_5_c, half_adder_6_c, half_adder_7_c,
       half_adder_8_c;

  Half_adder half_adder_1 (.A(in_1[7]), .B(half_adder_2_c), .Q(out_2[7]));  // open: C
  Half_adder half_adder_2 (.A(in_1[6]), .B(half_adder_3_c), .Q(out_2[6]), .C(half_adder_2_c));
  Half_adder half_adder_3 (.A(in_1[5]), .B(half_adder_4_c), .Q(out_2[5]), .C(half_adder_3_c));
  Half_adder half_adder_4 (.A(in_1[4]), .B(half_adder_5_c), .Q(out_2[4]), .C(half_adder_4_c));
  Half_adder half_adder_5 (.A(in_1[3]), .B(half_adder_6_c), .Q(out_2[3]), .C(half_adder_5_c));
  Half_adder half_adder_6 (.A(in_1[2]), .B(half_adder_7_c), .Q(out_2[2]), .C(half_adder_6_c));
  Half_adder half_adder_7 (.A(in_1[1]), .B(half_adder_8_c), .Q(out_2[1]), .C(half_adder_7_c));
  Half_adder half_adder_8 (.A(in_1[0]), .B(1'b1), .Q(out_2[0]), .C(half_adder_8_c));
endmodule

module MUX2x4 (
  input  [3:0] in_1,
  input  [3:0] in_2,
  input  in_3,
  output [3:0] out_4
);

  wire [3:0] and_1_out, and_2_out, not_1_out;

  assign not_1_out = ~{4{in_3}};  // NOT_Gate not_1, 4 bits wide
  assign and_1_out = not_1_out & in_1;  // AND_Gate and_1, 4 bits wide
  assign and_2_out = in_2 & {4{in_3}};  // AND_Gate and_2, 4 bits wide
  assign out_4 = and_1_out | and_2_out;  // OR_Gate or_1, 4 bits wide
endmodule

module MUX2x8 (
  input  [7:0] in_1,
  input  [7:0] in_2,
  input  in_3,
  output [7:0] out_4
);

  wire not_1_out;
  wire [7:0] mask8bit_1_out_3, mask8bit_2_out_3;

  Mask8bit mask8bit_1 (.in_1(in_1), .in_2(not_1_out), .out_3(mask8bit_1_out_3));
  Mask8bit mask8bit_2 (.in_1(in_2), .in_2(in_3), .out_3(mask8bit_2_out_3));
  not not_1 (not_1_out, in_3);
  assign out_4 = mask8bit_1_out_3 | mask8bit_2_out_3;  // OR_Gate or_1, 8 bits wide
endmodule

module Inc3bit (
  input  [2:0] in_1,
  output [2:0] out_2
);

  wire half_adder_2_c, half_adder_3_c;

  Half_adder half_adder_1 (.A(in_1[2]), .B(half_adder_2_c), .Q(out_2[2]));  // open: C
  Half_adder half_adder_2 (.A(in_1[1]), .B(half_adder_3_c), .Q(out_2[1]), .C(half_adder_2_c));
  Half_adder half_adder_3 (.A(in_1[0]), .B(1'b1), .Q(out_2[0]), .C(half_adder_3_c));
endmodule

module Comp3 (
  input  [2:0] in_1,
  input  [2:0] in_2,
  output out_3
);

  wire [2:0] xor_1_out;

  assign xor_1_out = in_1 ^ in_2;  // XOR_Gate xor_1, 3 bits wide
  nor nor_1 (out_3, xor_1_out[0], xor_1_out[1], xor_1_out[2]);
endmodule

module ClockDiv (
  input  Clock_input,
  input  [1:0] N_div_power,
  output Clock_output
);

  wire and_1_out, and_2_out, and_3_out, and_4_out, d_ff_1_q, d_ff_1_qn, d_ff_2_q, d_ff_2_qn, d_ff_3_q,
       d_ff_3_qn, d_ff_4_q, d_ff_4_qn, d_ff_5_q, d_ff_5_qn, d_ff_6_q, d_ff_6_qn, d_ff_7_q, d_ff_7_qn,
       d_ff_8_q, d_ff_8_qn, d_ff_9_q, d_ff_9_qn, d_ff_10_q, d_ff_10_qn, not_1_out, not_2_out, not_3_out,
       not_4_out;

  D_Flip_Flop d_ff_1 (.D(d_ff_1_qn), .clk(Clock_input), .Q(d_ff_1_q), .Qn(d_ff_1_qn));  // open: preset, reset
  D_Flip_Flop d_ff_2 (.D(d_ff_2_qn), .clk(Clock_input), .Q(d_ff_2_q), .Qn(d_ff_2_qn));  // open: preset, reset
  D_Flip_Flop d_ff_3 (.D(d_ff_3_qn), .clk(Clock_input), .Q(d_ff_3_q), .Qn(d_ff_3_qn));  // open: preset, reset
  D_Flip_Flop d_ff_4 (.D(d_ff_4_qn), .clk(Clock_input), .Q(d_ff_4_q), .Qn(d_ff_4_qn));  // open: preset, reset
  D_Flip_Flop d_ff_5 (.D(d_ff_5_qn), .clk(d_ff_2_q), .Q(d_ff_5_q), .Qn(d_ff_5_qn));  // open: preset, reset
  D_Flip_Flop d_ff_6 (.D(d_ff_6_qn), .clk(d_ff_3_q), .Q(d_ff_6_q), .Qn(d_ff_6_qn));  // open: preset, reset
  D_Flip_Flop d_ff_7 (.D(d_ff_7_qn), .clk(d_ff_4_q), .Q(d_ff_7_q), .Qn(d_ff_7_qn));  // open: preset, reset
  D_Flip_Flop d_ff_8 (.D(d_ff_8_qn), .clk(d_ff_6_q), .Q(d_ff_8_q), .Qn(d_ff_8_qn));  // open: preset, reset
  D_Flip_Flop d_ff_9 (.D(d_ff_9_qn), .clk(d_ff_7_q), .Q(d_ff_9_q), .Qn(d_ff_9_qn));  // open: preset, reset
  D_Flip_Flop d_ff_10 (.D(d_ff_10_qn), .clk(d_ff_9_q), .Q(d_ff_10_q), .Qn(d_ff_10_qn));  // open: preset, reset
  not not_1 (not_1_out, N_div_power[0]);
  not not_2 (not_2_out, N_div_power[1]);
  not not_3 (not_3_out, N_div_power[1]);
  not not_4 (not_4_out, N_div_power[0]);
  and and_1 (and_1_out, not_1_out, d_ff_1_q, not_2_out);
  and and_2 (and_2_out, N_div_power[0], d_ff_5_q, not_3_out);
  and and_3 (and_3_out, not_4_out, d_ff_8_q, N_div_power[1]);
  and and_4 (and_4_out, N_div_power[0], d_ff_10_q, N_div_power[1]);
  or or_1 (Clock_output, and_1_out, and_2_out, and_3_out, and_4_out);

  // Notes on the sheet:
  //   Divides the clock frequency by 2^n, where n is the 2bit input value
endmodule

module GameOverState (
  input  [1:0] current_state,
  input  Button1,
  input  Button2,
  input  [7:0] in_4,
  input  [7:0] in_5,
  input  [7:0] in_6,
  input  [7:0] in_7,
  input  [7:0] in_8,
  input  [7:0] in_9,
  input  [7:0] in_10,
  input  [7:0] in_11,
  input  [7:0] in_12,
  input  [7:0] in_13,
  input  [7:0] in_14,
  input  [7:0] in_15,
  input  [7:0] in_16,
  output [1:0] next_state,
  output GameReset,
  output [7:0] out_19,
  output [7:0] out_20,
  output [7:0] out_21,
  output [7:0] out_22,
  output [7:0] out_23,
  output [7:0] out_24,
  output [7:0] out_25,
  output [7:0] out_26,
  output [7:0] out_27,
  output [7:0] out_28,
  output [7:0] out_29,
  output [7:0] out_30
);

  wire active, not_2_out, or_1_out, s_r_ff_1_q;
  wire [7:0] display_number_1_four, display_number_1_one, display_number_1_three, display_number_1_two,
       display_number_1_zero, mask12x8_1_out_14, mask12x8_1_out_15, mask12x8_1_out_16, mask12x8_1_out_17,
       mask12x8_1_out_18, mask12x8_1_out_19, mask12x8_1_out_20, mask12x8_1_out_21, mask12x8_1_out_22,
       mask12x8_1_out_23, mask12x8_1_out_24, mask12x8_1_out_25, mask12x8_2_out_14, mask12x8_2_out_15,
       mask12x8_2_out_16, mask12x8_2_out_17, mask12x8_2_out_18, mask12x8_2_out_19, mask12x8_2_out_20,
       mask12x8_2_out_21, mask12x8_2_out_22, mask12x8_2_out_23, mask12x8_2_out_24, mask12x8_2_out_25;
  wire [11:11] not_1_out;

  Comp2 comp2_1 (.in_1(current_state), .in_2(2'b11), .out_3(active));
  not not_1 (not_1_out[11], active);
  display_number display_number_1 (
    .Zero(display_number_1_zero), .One(display_number_1_one), .Two(display_number_1_two),
    .Three(display_number_1_three), .Four(display_number_1_four), .High(in_4[7:4]), .Low(in_4[3:0]));
  Mask12x8 mask12x8_1 (
    .in_1(in_5), .in_2(in_6), .in_3(in_7), .in_4(in_8), .in_5(in_9), .in_6(in_10), .in_7(in_11),
    .in_8(in_12), .in_9(in_13), .in_10(in_14), .in_11(in_15), .in_12(in_16), .in_13({12{not_1_out[11]}}),
    .out_14(mask12x8_1_out_14), .out_15(mask12x8_1_out_15), .out_16(mask12x8_1_out_16),
    .out_17(mask12x8_1_out_17), .out_18(mask12x8_1_out_18), .out_19(mask12x8_1_out_19),
    .out_20(mask12x8_1_out_20), .out_21(mask12x8_1_out_21), .out_22(mask12x8_1_out_22),
    .out_23(mask12x8_1_out_23), .out_24(mask12x8_1_out_24), .out_25(mask12x8_1_out_25));
  or or_1 (or_1_out, Button1, Button2);
  S_R_Flip_Flop s_r_ff_1 (.Q(s_r_ff_1_q), .reset(not_2_out), .preset(or_1_out));  // open: S, R, clk, Qn
  not not_2 (not_2_out, active);
  Mask12x8 mask12x8_2 (
    .in_1({8{1'b0}}), .in_2({8{1'b0}}), .in_3({8{1'b0}}), .in_4(display_number_1_zero),
    .in_5(display_number_1_one), .in_6(display_number_1_two), .in_7(display_number_1_three),
    .in_8(display_number_1_four), .in_9({8{1'b0}}), .in_10({8{1'b0}}), .in_11({8{1'b0}}), .in_12({8{1'b0}}),
    .in_13({12{active}}), .out_14(mask12x8_2_out_14), .out_15(mask12x8_2_out_15), .out_16(mask12x8_2_out_16),
    .out_17(mask12x8_2_out_17), .out_18(mask12x8_2_out_18), .out_19(mask12x8_2_out_19),
    .out_20(mask12x8_2_out_20), .out_21(mask12x8_2_out_21), .out_22(mask12x8_2_out_22),
    .out_23(mask12x8_2_out_23), .out_24(mask12x8_2_out_24), .out_25(mask12x8_2_out_25));
  OR12 or12_1 (
    .in_13(mask12x8_1_out_14), .in_14(mask12x8_1_out_15), .in_15(mask12x8_1_out_16),
    .in_16(mask12x8_1_out_17), .in_17(mask12x8_1_out_18), .in_18(mask12x8_1_out_19),
    .in_19(mask12x8_1_out_20), .in_20(mask12x8_1_out_21), .in_21(mask12x8_1_out_22),
    .in_22(mask12x8_1_out_23), .in_23(mask12x8_1_out_24), .in_24(mask12x8_1_out_25),
    .in_1(mask12x8_2_out_14), .in_2(mask12x8_2_out_15), .in_3(mask12x8_2_out_16), .in_4(mask12x8_2_out_17),
    .in_5(mask12x8_2_out_18), .in_6(mask12x8_2_out_19), .in_7(mask12x8_2_out_20), .in_8(mask12x8_2_out_21),
    .in_9(mask12x8_2_out_22), .in_10(mask12x8_2_out_23), .in_11(mask12x8_2_out_24),
    .in_12(mask12x8_2_out_25), .out_25(out_19), .out_26(out_20), .out_27(out_21), .out_28(out_22),
    .out_29(out_23), .out_30(out_24), .out_31(out_25), .out_32(out_26), .out_33(out_27), .out_34(out_28),
    .out_35(out_29), .out_36(out_30));
  MUX2x2 mux2x2_1 (.in_1(2'b11), .in_2(2'b00), .in_3(s_r_ff_1_q), .out_4(next_state));
  and and_1 (GameReset, s_r_ff_1_q, active);

  // Notes on the sheet:
  //   score
endmodule

module LED_Connector (
  input  [7:0] in_1,
  output out_2,
  output out_3,
  output out_4,
  output out_5,
  output out_6,
  output out_7,
  output out_8,
  output out_9
);


  assign out_2 = in_1[7];
  assign out_3 = in_1[6];
  assign out_4 = in_1[5];
  assign out_5 = in_1[4];
  assign out_6 = in_1[3];
  assign out_7 = in_1[2];
  assign out_8 = in_1[1];
  assign out_9 = in_1[0];
endmodule

module Comp4 (
  input  [3:0] in_1,
  input  [3:0] in_2,
  output out_3
);

  wire [3:0] xor_1_out;

  assign xor_1_out = in_1 ^ in_2;  // XOR_Gate xor_1, 4 bits wide
  nor nor_1 (out_3, xor_1_out[0], xor_1_out[1], xor_1_out[2], xor_1_out[3]);
endmodule

module Inc4bit (
  input  [3:0] in_1,
  output [3:0] out_2
);

  wire half_adder_2_c, half_adder_3_c, half_adder_4_c;

  Half_adder half_adder_1 (.A(in_1[3]), .B(half_adder_2_c), .Q(out_2[3]));  // open: C
  Half_adder half_adder_2 (.A(in_1[2]), .B(half_adder_3_c), .Q(out_2[2]), .C(half_adder_2_c));
  Half_adder half_adder_3 (.A(in_1[1]), .B(half_adder_4_c), .Q(out_2[1]), .C(half_adder_3_c));
  Half_adder half_adder_4 (.A(in_1[0]), .B(1'b1), .Q(out_2[0]), .C(half_adder_4_c));
endmodule

module PlayerState (
  input  [1:0] current_state,
  input  [7:0] read_line,
  input  in_3,
  output [1:0] next_state,
  output [7:0] Player,
  output [3:0] out_6,
  output [3:0] read_addr
);

  wire active, and_2_out, and_5_out, comp2_2_out_3, comp2_3_out_3, comp2_4_out_3, comp4_1_out_3, not_1_out,
       not_2_out, or_1_out, PlayerBlocked, PlayerReset;
  wire [1:0] inc2bit_1_out_2, LocalState, mux2x2_1_out_4;
  wire [3:0] mux2x4_1_out_4, NextLineNumber;
  wire [7:0] and_1_out;

  Comp2 comp2_1 (.in_1(current_state), .in_2(2'b00), .out_3(active));
  Register #(.width(2)) register_1 (.D(inc2bit_1_out_2), .en(1'b1), .clk(in_3), .Q(LocalState), .clr(not_1_out));
  Inc2bit inc2bit_1 (.in_1(LocalState), .out_2(inc2bit_1_out_2));
  assign and_1_out = read_line & 8'h10;  // AND_Gate and_1, 8 bits wide
  not not_1 (not_1_out, active);
  or or_1 (or_1_out, and_1_out[0], and_1_out[1], and_1_out[2], and_1_out[3], and_1_out[4], and_1_out[5], and_1_out[6], and_1_out[7]);
  Comp4 comp4_1 (.in_1(out_6), .in_2(4'b1011), .out_3(comp4_1_out_3));
  or or_2 (PlayerBlocked, or_1_out, comp4_1_out_3);
  Comp2 comp2_2 (.in_1(LocalState), .in_2(2'b10), .out_3(comp2_2_out_3));
  and and_2 (and_2_out, comp2_2_out_3, active);
  MUX2x2 mux2x2_1 (.in_1(2'b00), .in_2(2'b10), .in_3(PlayerBlocked), .out_4(mux2x2_1_out_4));
  Comp2 comp2_3 (.in_1(LocalState), .in_2(2'b00), .out_3(comp2_3_out_3));
  Comp2 comp2_4 (.in_1(LocalState), .in_2(2'b00), .out_3(comp2_4_out_3));
  MUX2x4 mux2x4_1 (.in_1(out_6), .in_2(NextLineNumber), .in_3(not_2_out), .out_4(mux2x4_1_out_4));
  not not_2 (not_2_out, PlayerBlocked);
  and and_3 (PlayerReset, comp2_3_out_3, active);
  // AND_Gate and_4 has open pins: in0=comp2_4_out_3, in1=active, out=open
  Register #(.width(4)) register_2 (.D(mux2x4_1_out_4), .en(and_5_out), .clk(in_3), .Q(out_6), .clr(PlayerReset));
  and and_5 (and_5_out, not_2_out, and_2_out);
  MUX2x4 mux2x4_2 (.in_1(out_6), .in_2(NextLineNumber), .in_3(and_2_out), .out_4(read_addr));
  MUX4x2 mux4x2_1 (
    .in_1(2'b00), .in_2(2'b00), .in_3(mux2x2_1_out_4), .in_5(LocalState), .out_6(next_state));  // open: in_4
  Inc4bit inc4bit_1 (.in_1(out_6), .out_2(NextLineNumber));

  assign Player = 8'h10;

  // Other names for the same wires on the sheet: clock = in_3; CurrentLineNumber[3:0] = out_6

  // Notes on the sheet:
  //   local state variable
  //   PlayerState
  //   BlockWriteState
  //   At state 0 reset the line
  //   current line variable
endmodule

module Line_Check (
  input  [7:0] Player,
  input  [7:0] Memory_Line,
  output right_blocked,
  output left_blocked
);

  wire [7:0] and_1_out, and_2_out;

  assign and_1_out = Player & {1'b1, Memory_Line[7:1]};  // AND_Gate and_1, 8 bits wide
  assign and_2_out = Player & {Memory_Line[6:0], 1'b1};  // AND_Gate and_2, 8 bits wide
  or or_1 (right_blocked, and_2_out[0], and_2_out[1], and_2_out[2], and_2_out[3], and_2_out[4], and_2_out[5], and_2_out[6], and_2_out[7]);
  or or_2 (left_blocked, and_1_out[0], and_1_out[1], and_1_out[2], and_1_out[3], and_1_out[4], and_1_out[5], and_1_out[6], and_1_out[7]);
endmodule

module hor_freedom (
  input  right_blocked,
  input  left_blocked,
  input  right_button,
  input  left_button,
  output right,
  output straight,
  output left
);

  wire and_2_out, and_3_out, not_1_out, not_2_out, not_3_out, not_4_out, not_5_out, xor_1_out;

  not not_1 (not_1_out, right_blocked);
  not not_2 (not_2_out, left_button);
  not not_3 (not_3_out, right_button);
  not not_4 (not_4_out, left_blocked);
  and and_1 (right, not_1_out, right_button, not_2_out);
  and and_2 (and_2_out, right_blocked, right_button);
  not not_5 (not_5_out, xor_1_out);
  xor xor_1 (xor_1_out, right_button, left_button);
  and and_3 (and_3_out, left_button, left_blocked);
  and and_4 (left, left_button, not_3_out, not_4_out);
  or or_1 (straight, and_2_out, not_5_out, and_3_out);
endmodule

module hor_movement (
  input  [7:0] data_line,
  input  right_button,
  input  left_button,
  input  select,
  input  clock,
  input  reset,
  output [7:0] player
);

  wire line_check_1_left_blocked, line_check_1_right_blocked;
  wire [7:0] and_1_out, and_2_out, and_3_out, or_1_out, rand_generator_1_output;
  wire [7:7] hor_freedom_1_left, hor_freedom_1_right, hor_freedom_1_straight;

  Register register_1 (.D(rand_generator_1_output), .en(select), .clk(clock), .Q(player), .clr(reset));
  Line_Check line_check_1 (
    .Player(player), .Memory_Line(data_line), .right_blocked(line_check_1_right_blocked),
    .left_blocked(line_check_1_left_blocked));
  rand_generator rand_generator_1 (.\input (or_1_out), .clock(clock), .\output (rand_generator_1_output));
  hor_freedom hor_freedom_1 (
    .right_blocked(line_check_1_right_blocked), .left_blocked(line_check_1_left_blocked),
    .right_button(right_button), .left_button(left_button), .right(hor_freedom_1_right[7]),
    .straight(hor_freedom_1_straight[7]), .left(hor_freedom_1_left[7]));
  assign and_1_out = {1'b0, player[7:1]} & {8{hor_freedom_1_right[7]}};  // AND_Gate and_1, 8 bits wide
  assign and_2_out = player & {8{hor_freedom_1_straight[7]}};  // AND_Gate and_2, 8 bits wide
  assign and_3_out = {player[6:0], 1'b0} & {8{hor_freedom_1_left[7]}};  // AND_Gate and_3, 8 bits wide
  assign or_1_out = and_1_out | and_2_out | and_3_out;  // OR_Gate or_1, 8 bits wide
endmodule

module rand_generator (
  input  [7:0] \input ,
  input  clock,
  output [7:0] \output 
);

  wire undriven;
  wire [2:0] random_1_out;
  wire [7:0] and_1_out, and_2_out, bin_onehot_1_output;
  wire [7:7] not_1_out, or_1_out;

  or or_1 (or_1_out[7], \input [0], \input [1], \input [2], \input [3], \input [4], \input [5], \input [6], \input [7]);
  assign and_1_out = \input  & {8{or_1_out[7]}};  // AND_Gate and_1, 8 bits wide
  not not_1 (not_1_out[7], or_1_out[7]);
  assign and_2_out = bin_onehot_1_output & {8{not_1_out[7]}};  // AND_Gate and_2, 8 bits wide
  assign \output  = and_1_out | and_2_out;  // OR_Gate or_2, 8 bits wide
  Random #(.width(3)) random_1 (.clr(undriven), .next(not_1_out[7]), .clk(clock), .out(random_1_out));
  bin_onehot bin_onehot_1 (.\input (random_1_out), .\output (bin_onehot_1_output));
endmodule

module bin_onehot (
  input  [2:0] \input ,
  output [7:0] \output 
);

  wire not_1_out, not_2_out, not_3_out, not_4_out, not_5_out, not_6_out, not_7_out, not_8_out, not_9_out,
       not_10_out, not_11_out, not_12_out;

  and and_1 (\output [7], \input [2], \input [1], \input [0]);
  not not_1 (not_1_out, \input [0]);
  not not_2 (not_2_out, \input [1]);
  not not_3 (not_3_out, \input [1]);
  not not_4 (not_4_out, \input [0]);
  not not_5 (not_5_out, \input [2]);
  not not_6 (not_6_out, \input [2]);
  not not_7 (not_7_out, \input [0]);
  not not_8 (not_8_out, \input [2]);
  not not_9 (not_9_out, \input [1]);
  not not_10 (not_10_out, \input [2]);
  not not_11 (not_11_out, \input [1]);
  not not_12 (not_12_out, \input [0]);
  and and_2 (\output [6], \input [2], \input [1], not_1_out);
  and and_3 (\output [5], \input [2], not_2_out, \input [0]);
  and and_4 (\output [4], \input [2], not_3_out, not_4_out);
  and and_5 (\output [3], not_5_out, \input [1], \input [0]);
  and and_6 (\output [2], not_6_out, \input [1], not_7_out);
  and and_7 (\output [1], not_8_out, not_9_out, \input [0]);
  and and_8 (\output [0], not_10_out, not_11_out, not_12_out);
endmodule

module check_down (
  input  [7:0] player,
  input  [7:0] next_line,
  output next_line_blocked
);

  wire [7:0] and_1_out;

  assign and_1_out = player & next_line;  // AND_Gate and_1, 8 bits wide
  or or_1 (next_line_blocked, and_1_out[0], and_1_out[1], and_1_out[2], and_1_out[3], and_1_out[4], and_1_out[5], and_1_out[6], and_1_out[7]);
endmodule

module player (
  input  [7:0] data_line,
  input  right_button,
  input  left_button,
  input  clock,
  input  reset,
  input  [3:0] nb_side,
  input  [2:0] current_state,
  output [7:0] player_out,
  output [2:0] next_state
);

  wire d_ff_1_q, or_1_out;
  wire [2:0] and_1_out, and_2_out;
  wire [2:2] comparator3_1_equal, comparator_1_equal;
  wire [3:0] counter_1_counter;

  or or_1 (or_1_out, d_ff_1_q, reset);
  comparator3 comparator3_1 (.A(current_state), .B(3'b010), .equal(comparator3_1_equal[2]));
  counter counter_1 (.clock(clock), .reset(or_1_out), .counter(counter_1_counter), .enable(comparator3_1_equal[2]));
  // Probe on counter_1_counter
  comparator comparator_1 (.counter(counter_1_counter), .comp_val(nb_side), .equal(comparator_1_equal[2]));
  hor_movement hor_movement_1 (
    .data_line(data_line), .right_button(right_button), .left_button(left_button),
    .select(comparator3_1_equal[2]), .clock(clock), .reset(reset), .player(player_out));
  D_Flip_Flop d_ff_1 (.D(comparator_1_equal[2]), .clk(clock), .Q(d_ff_1_q), .reset(reset));  // open: Qn, preset
  assign and_1_out = {3{comparator3_1_equal[2]}} & 3'b010;  // AND_Gate and_1, 3 bits wide
  assign next_state = and_1_out | and_2_out;  // OR_Gate or_2, 3 bits wide
  assign and_2_out = 3'b011 & {3{comparator_1_equal[2]}};  // AND_Gate and_2, 3 bits wide
endmodule

module counter (
  input  enable,
  input  clock,
  input  reset,
  output [3:0] counter
);

  wire adder_1_o, adder_2_cout, adder_2_o, adder_3_cout, adder_3_o, adder_4_cout, adder_4_o;

  Adder adder_1 (.A(1'b0), .B(counter[3]), .Cin(adder_2_cout), .O(adder_1_o));  // open: Cout
  Adder adder_2 (.A(1'b0), .B(counter[2]), .Cin(adder_3_cout), .Cout(adder_2_cout), .O(adder_2_o));
  Adder adder_3 (.A(1'b0), .B(counter[1]), .Cin(adder_4_cout), .Cout(adder_3_cout), .O(adder_3_o));
  Adder adder_4 (.A(1'b0), .B(counter[0]), .Cin(enable), .Cout(adder_4_cout), .O(adder_4_o));
  D_Flip_Flop d_ff_1 (.D(adder_1_o), .clk(clock), .Q(counter[3]), .reset(reset));  // open: Qn, preset
  D_Flip_Flop d_ff_2 (.D(adder_2_o), .clk(clock), .Q(counter[2]), .reset(reset));  // open: Qn, preset
  D_Flip_Flop d_ff_3 (.D(adder_3_o), .clk(clock), .Q(counter[1]), .reset(reset));  // open: Qn, preset
  D_Flip_Flop d_ff_4 (.D(adder_4_o), .clk(clock), .Q(counter[0]), .reset(reset));  // open: Qn, preset
endmodule

module Half_adder (
  input  A,
  input  B,
  output Q,
  output C
);

  xor xor_1 (Q, B, A);
  and and_1 (C, A, B);
endmodule

module Adder (
  input  A,
  input  B,
  input  Cin,
  output Cout,
  output O
);

  wire half_adder_1_c, half_adder_1_q, half_adder_2_c;

  Half_adder half_adder_1 (.A(A), .B(B), .Q(half_adder_1_q), .C(half_adder_1_c));
  Half_adder half_adder_2 (.A(half_adder_1_q), .B(Cin), .Q(O), .C(half_adder_2_c));
  or or_1 (Cout, half_adder_1_c, half_adder_2_c);
endmodule

module comparator (
  input  [3:0] counter,
  input  [3:0] comp_val,
  output equal
);

  wire [3:0] not_1_out, xor_1_out;

  assign xor_1_out = counter ^ comp_val;  // XOR_Gate xor_1, 4 bits wide
  assign not_1_out = ~xor_1_out;  // NOT_Gate not_1, 4 bits wide
  and and_1 (equal, not_1_out[0], not_1_out[1], not_1_out[2], not_1_out[3]);
endmodule

// current_state
module block_set (
  input  [2:0] line_nbr,
  input  [1:0] current_state,
  output write,
  output player_reset,
  output [1:0] next_state
);

  wire and_1_out;
  wire [1:0] and_2_out, and_4_out, and_5_out, not_1_out, not_3_out, xor_1_out;
  wire [1:1] and_3_out, undriven;
  wire [2:0] not_2_out, xor_2_out;

  assign xor_1_out = current_state ^ 2'b01;  // XOR_Gate xor_1, 2 bits wide
  and and_1 (and_1_out, not_1_out[0], not_1_out[1]);
  assign not_1_out = ~xor_1_out;  // NOT_Gate not_1, 2 bits wide
  counter counter_1 (.enable(and_1_out));  // open: clock, reset, counter
  assign xor_2_out = line_nbr ^ 3'b000;  // XOR_Gate xor_2, 3 bits wide
  assign not_2_out = ~xor_2_out;  // NOT_Gate not_2, 3 bits wide
  assign and_2_out = 2'b11 & {2{and_3_out[1]}};  // AND_Gate and_2, 2 bits wide
  and and_3 (and_3_out[1], not_2_out[0], not_2_out[1], not_2_out[2]);
  assign and_4_out = 2'b01 & not_3_out;  // AND_Gate and_4, 2 bits wide
  assign not_3_out = ~{2{undriven[1]}};  // NOT_Gate not_3, 2 bits wide
  assign and_5_out = {2{undriven[1]}} & and_2_out;  // AND_Gate and_5, 2 bits wide
  assign next_state = and_4_out | and_5_out;  // OR_Gate or_1, 2 bits wide
endmodule

module comparator3 (
  input  [2:0] A,
  input  [2:0] B,
  output equal
);

  wire [2:0] not_1_out, xor_1_out;

  assign xor_1_out = A ^ B;  // XOR_Gate xor_1, 3 bits wide
  and and_1 (equal, not_1_out[0], not_1_out[1], not_1_out[2]);
  assign not_1_out = ~xor_1_out;  // NOT_Gate not_1, 3 bits wide
endmodule

module read_current_line (
  input  [2:0] current_state,
  input  clock,
  input  [7:0] data_in,
  input  reset,
  input  [3:0] line_in,
  output [2:0] next_state,
  output [7:0] data_out,
  output [3:0] line_out
);

  wire not_1_out;
  wire [2:0] and_3_out, and_4_out, and_5_out, not_2_out;
  wire [2:2] and_2_out, d_ff_1_q;
  wire [3:3] comparator3_1_equal;

  D_Flip_Flop d_ff_1 (.D(comparator3_1_equal[3]), .clk(clock), .Q(d_ff_1_q[2]), .reset(reset));  // open: Qn, preset
  comparator3 comparator3_1 (.A(current_state), .B(3'b001), .equal(comparator3_1_equal[3]));
  Register register_1 (.D(data_in), .en(comparator3_1_equal[3]), .clk(clock), .Q(data_out), .clr(reset));
  assign line_out = {4{comparator3_1_equal[3]}} & line_in;  // AND_Gate and_1, 4 bits wide
  and and_2 (and_2_out[2], comparator3_1_equal[3], not_1_out);
  not not_1 (not_1_out, d_ff_1_q[2]);
  assign and_3_out = 3'b001 & {3{and_2_out[2]}};  // AND_Gate and_3, 3 bits wide
  assign and_4_out = 3'b010 & {3{d_ff_1_q[2]}};  // AND_Gate and_4, 3 bits wide
  assign and_5_out = 3'b000 & not_2_out;  // AND_Gate and_5, 3 bits wide
  assign not_2_out = ~{3{d_ff_1_q[2]}};  // NOT_Gate not_2, 3 bits wide
  assign next_state = and_3_out | and_4_out | and_5_out;  // OR_Gate or_1, 3 bits wide
endmodule

module read_next_line (
  input  [2:0] current_state,
  input  clock,
  input  [7:0] data_in,
  input  reset,
  input  [3:0] line_in,
  output [2:0] next_state,
  output [7:0] data_out,
  output [3:0] line_out
);

  wire not_1_out;
  wire [2:0] and_3_out, and_4_out, and_5_out, not_2_out;
  wire [2:2] and_2_out, d_ff_1_q;
  wire [3:0] adder4_1_o;
  wire [3:3] comparator3_1_equal;

  comparator3 comparator3_1 (.A(current_state), .B(3'b011), .equal(comparator3_1_equal[3]));
  D_Flip_Flop d_ff_1 (.D(comparator3_1_equal[3]), .clk(clock), .Q(d_ff_1_q[2]), .reset(reset));  // open: Qn, preset
  Register register_1 (.D(data_in), .en(comparator3_1_equal[3]), .clk(clock), .Q(data_out), .clr(reset));
  adder4 adder4_1 (.A(4'b0001), .B(line_in), .O(adder4_1_o));
  not not_1 (not_1_out, d_ff_1_q[2]);
  assign line_out = {4{comparator3_1_equal[3]}} & adder4_1_o;  // AND_Gate and_1, 4 bits wide
  and and_2 (and_2_out[2], comparator3_1_equal[3], not_1_out);
  assign not_2_out = ~{3{d_ff_1_q[2]}};  // NOT_Gate not_2, 3 bits wide
  assign and_3_out = {3{and_2_out[2]}} & 3'b011;  // AND_Gate and_3, 3 bits wide
  assign and_4_out = {3{d_ff_1_q[2]}} & 3'b100;  // AND_Gate and_4, 3 bits wide
  assign next_state = and_3_out | and_4_out | and_5_out;  // OR_Gate or_1, 3 bits wide
  assign and_5_out = 3'b000 & not_2_out;  // AND_Gate and_5, 3 bits wide
endmodule

module player_fsm (
  input  right_button,
  input  left_button,
  input  [3:0] nb_side,
  input  [7:0] data_line,
  input  [1:0] current_state2,
  input  reset,
  input  clock,
  output [7:0] player,
  output [3:0] read_line,
  output [3:0] player_line,
  output [1:0] next_state2
);

  wire or_1_out, set_next_state_1_active, set_next_state_1_reset_state;
  wire [2:0] blocked_1_next_state, line_nbr_plus_1_next_state, mux6x3_1_out_8, player_1_next_state,
       read_current_line_1_next_state, read_next_line_1_next_state, register_1_q,
       set_next_state_1_current_state3_2;
  wire [3:0] read_current_line_1_line_out, read_next_line_1_line_out;
  wire [7:0] read_current_line_1_data_out, read_next_line_1_data_out;

  // Probe on player_line
  read_current_line read_current_line_1 (
    .current_state(register_1_q), .clock(clock), .data_in(data_line), .reset(reset), .line_in(player_line),
    .next_state(read_current_line_1_next_state), .data_out(read_current_line_1_data_out),
    .line_out(read_current_line_1_line_out));
  read_next_line read_next_line_1 (
    .current_state(register_1_q), .clock(clock), .data_in(data_line), .reset(reset), .line_in(player_line),
    .next_state(read_next_line_1_next_state), .data_out(read_next_line_1_data_out),
    .line_out(read_next_line_1_line_out));
  line_nbr_plus line_nbr_plus_1 (
    .reset(reset), .current_state(register_1_q), .next_state(line_nbr_plus_1_next_state),
    .line_nbr(player_line));
  // Probe on player
  player player_1 (
    .data_line(read_current_line_1_data_out), .right_button(right_button), .left_button(left_button),
    .clock(clock), .reset(reset), .nb_side(nb_side), .current_state(register_1_q), .player_out(player),
    .next_state(player_1_next_state));
  blocked blocked_1 (
    .player(player), .next_line(read_next_line_1_data_out), .current_state(register_1_q),
    .next_state(blocked_1_next_state), .line_nbr(player_line));
  set_next_state set_next_state_1 (
    .current_state3(register_1_q), .reset(reset), .clock(clock), .current_state2(current_state2),
    .current_state3_2(set_next_state_1_current_state3_2), .current_state2_2(next_state2),
    .active(set_next_state_1_active), .reset_state(set_next_state_1_reset_state));
  // Probe on player_1_next_state
  // Probe on read_next_line_1_next_state
  // Probe on blocked_1_next_state
  // Probe on line_nbr_plus_1_next_state
  // Probe on set_next_state_1_current_state3_2
  // Probe on read_current_line_1_next_state
  // Probe on register_1_q
  // Probe on mux6x3_1_out_8
  MUX6x3 mux6x3_1 (
    .in_1(read_current_line_1_next_state), .in_2(player_1_next_state), .in_3(read_next_line_1_next_state),
    .in_4(blocked_1_next_state), .in_5(line_nbr_plus_1_next_state), .in_6(set_next_state_1_current_state3_2),
    .current_state(register_1_q), .out_8(mux6x3_1_out_8));
  Register #(.width(3)) register_1 (
    .D(mux6x3_1_out_8), .en(set_next_state_1_active), .clk(clock), .Q(register_1_q), .clr(or_1_out));
  or or_1 (or_1_out, set_next_state_1_reset_state, reset);
  assign read_line = read_current_line_1_line_out | read_next_line_1_line_out;  // OR_Gate or_2, 4 bits wide
endmodule

module line_counter (
  input  plusone,
  input  reset,
  output [3:0] line_nbr
);

  wire half_adder_1_q, half_adder_2_c, half_adder_2_q, half_adder_3_c, half_adder_3_q, half_adder_4_c,
       half_adder_4_q;

  Half_adder half_adder_1 (.A(line_nbr[3]), .B(half_adder_2_c), .Q(half_adder_1_q));  // open: C
  Half_adder half_adder_2 (.A(line_nbr[2]), .B(half_adder_3_c), .Q(half_adder_2_q), .C(half_adder_2_c));
  Half_adder half_adder_3 (.A(line_nbr[1]), .B(half_adder_4_c), .Q(half_adder_3_q), .C(half_adder_3_c));
  Half_adder half_adder_4 (.A(line_nbr[0]), .B(1'b1), .Q(half_adder_4_q), .C(half_adder_4_c));
  D_Flip_Flop d_ff_1 (.D(half_adder_1_q), .clk(plusone), .Q(line_nbr[3]), .reset(reset));  // open: Qn, preset
  D_Flip_Flop d_ff_2 (.D(half_adder_2_q), .clk(plusone), .Q(line_nbr[2]), .reset(reset));  // open: Qn, preset
  D_Flip_Flop d_ff_3 (.D(half_adder_3_q), .clk(plusone), .Q(line_nbr[1]), .reset(reset));  // open: Qn, preset
  D_Flip_Flop d_ff_4 (.D(half_adder_4_q), .clk(plusone), .Q(line_nbr[0]), .reset(reset));  // open: Qn, preset
endmodule

module blocked (
  input  [7:0] player,
  input  [7:0] next_line,
  input  [3:0] line_nbr,
  input  [2:0] current_state,
  output [2:0] next_state
);

  wire comparator_1_equal, or_1_out, or_2_out;
  wire [2:0] and_3_out, and_4_out, not_1_out, or_3_out;
  wire [2:2] and_2_out, comparator3_1_equal;
  wire [7:0] and_1_out;

  assign and_1_out = player & next_line;  // AND_Gate and_1, 8 bits wide
  comparator comparator_1 (.counter(line_nbr), .comp_val(4'b1011), .equal(comparator_1_equal));
  comparator3 comparator3_1 (.A(current_state), .B(3'b100), .equal(comparator3_1_equal[2]));
  or or_1 (or_1_out, and_1_out[0], and_1_out[1], and_1_out[2], and_1_out[3], and_1_out[4], and_1_out[5], and_1_out[6], and_1_out[7]);
  or or_2 (or_2_out, or_1_out, comparator_1_equal);
  and and_2 (and_2_out[2], or_2_out, comparator3_1_equal[2]);
  assign and_3_out = {3{and_2_out[2]}} & 3'b110;  // AND_Gate and_3, 3 bits wide
  assign not_1_out = ~{3{and_2_out[2]}};  // NOT_Gate not_1, 3 bits wide
  assign and_4_out = not_1_out & 3'b101;  // AND_Gate and_4, 3 bits wide
  assign or_3_out = and_3_out | and_4_out;  // OR_Gate or_3, 3 bits wide
  assign next_state = or_3_out & {3{comparator3_1_equal[2]}};  // AND_Gate and_5, 3 bits wide
endmodule

module line_nbr_plus (
  input  reset,
  input  [2:0] current_state,
  output [3:0] line_nbr,
  output [2:0] next_state
);

  wire [2:2] comparator3_1_equal;

  comparator3 comparator3_1 (.A(current_state), .B(3'b101), .equal(comparator3_1_equal[2]));
  line_counter line_counter_1 (.plusone(comparator3_1_equal[2]), .line_nbr(line_nbr), .reset(reset));
  assign next_state = {3{comparator3_1_equal[2]}} & 3'b001;  // AND_Gate and_1, 3 bits wide
endmodule

module adder4 (
  input  [3:0] A,
  input  [3:0] B,
  output [3:0] O
);

  wire adder_3_cout, adder_4_cout;

  Adder adder_1 (.A(A[3]), .B(B[3]), .O(O[3]));  // open: Cin, Cout
  Adder adder_2 (.A(A[2]), .B(B[2]), .Cin(adder_3_cout), .Cout(O[2]));  // open: O
  Adder adder_3 (.A(A[1]), .B(B[1]), .Cin(adder_4_cout), .Cout(adder_3_cout), .O(O[1]));
  Adder adder_4 (.A(A[0]), .B(B[0]), .Cin(1'b0), .Cout(adder_4_cout), .O(O[0]));
endmodule

module set_next_state (
  input  [2:0] current_state3,
  input  reset,
  input  clock,
  input  [1:0] current_state2,
  output [2:0] current_state3_2,
  output [1:0] current_state2_2,
  output reset_state,
  output active
);

  wire comparator3_1_equal;
  wire [1:0] not_1_out, xor_1_out;
  wire [1:1] comparator3_2_equal;
  wire [2:0] and_3_out, and_4_out;
  wire [2:2] and_2_out;

  comparator3 comparator3_1 (.A(current_state3), .B(3'b000), .equal(comparator3_1_equal));
  comparator3 comparator3_2 (.A(current_state3), .B(3'b110), .equal(comparator3_2_equal[1]));
  assign not_1_out = ~xor_1_out;  // NOT_Gate not_1, 2 bits wide
  assign xor_1_out = current_state2 ^ 2'b00;  // XOR_Gate xor_1, 2 bits wide
  and and_1 (active, not_1_out[0], not_1_out[1]);
  and and_2 (and_2_out[2], comparator3_1_equal, active);
  D_Flip_Flop d_ff_1 (.D(comparator3_2_equal[1]), .clk(clock), .Q(reset_state), .reset(reset));  // open: Qn, preset
  assign and_3_out = {3{comparator3_2_equal[1]}} & 3'b000;  // AND_Gate and_3, 3 bits wide
  assign and_4_out = 3'b001 & {3{and_2_out[2]}};  // AND_Gate and_4, 3 bits wide
  assign current_state2_2 = {2{comparator3_2_equal[1]}} & 2'b01;  // AND_Gate and_5, 2 bits wide
  assign current_state3_2 = and_3_out | and_4_out;  // OR_Gate or_1, 3 bits wide
endmodule

module display_number (
  input  [3:0] High,
  input  [3:0] Low,
  output [7:0] Zero,
  output [7:0] One,
  output [7:0] Two,
  output [7:0] Three,
  output [7:0] Four
);

  wire and_1_out, and_2_out, and_3_out, and_4_out, and_5_out, and_6_out, and_7_out, and_8_out, and_9_out,
       and_10_out, and_11_out, and_12_out, and_13_out, and_14_out, and_15_out, and_16_out, and_17_out,
       and_18_out, and_19_out, and_20_out, and_21_out, and_22_out, and_23_out, and_24_out, and_25_out,
       and_26_out, and_27_out, and_28_out, and_29_out, and_30_out, and_31_out, and_32_out, and_33_out,
       and_34_out, and_35_out, and_36_out, and_37_out, and_38_out, and_39_out, and_40_out, and_41_out,
       and_42_out, and_43_out, and_44_out, and_45_out, and_46_out, and_47_out, and_48_out, and_49_out,
       and_50_out, and_51_out, and_52_out, not_1_out, not_2_out, not_3_out, not_4_out, not_5_out, not_6_out,
       not_7_out, not_8_out, not_9_out, not_10_out, not_11_out, not_12_out, not_13_out, not_14_out,
       not_15_out, not_16_out, not_17_out, not_18_out, not_19_out, not_20_out, not_21_out, not_22_out,
       not_23_out, not_24_out, not_25_out, not_26_out, not_27_out, not_28_out, not_29_out, not_30_out,
       not_31_out, not_32_out, not_33_out, not_34_out, not_35_out, not_36_out, not_37_out, not_38_out,
       not_39_out, not_40_out, not_41_out, not_42_out, not_43_out, not_44_out, not_45_out, not_46_out,
       not_47_out, not_48_out, not_49_out, not_50_out, not_51_out, not_52_out, not_53_out, not_54_out,
       not_55_out, not_56_out, not_57_out, not_58_out, not_59_out, not_60_out, not_61_out, not_62_out,
       not_63_out, not_64_out, not_65_out, not_66_out, not_67_out, not_68_out, not_69_out, not_70_out;

  not not_1 (not_1_out, High[0]);
  not not_2 (not_2_out, High[2]);
  not not_3 (not_3_out, High[0]);
  not not_4 (not_4_out, High[1]);
  not not_5 (not_5_out, High[0]);
  not not_6 (not_6_out, High[1]);
  not not_7 (not_7_out, High[0]);
  not not_8 (not_8_out, High[1]);
  not not_9 (not_9_out, High[0]);
  not not_10 (not_10_out, High[2]);
  not not_11 (not_11_out, High[1]);
  not not_12 (not_12_out, High[2]);
  not not_13 (not_13_out, High[1]);
  not not_14 (not_14_out, High[0]);
  not not_15 (not_15_out, High[2]);
  not not_16 (not_16_out, High[1]);
  not not_17 (not_17_out, High[0]);
  not not_18 (not_18_out, High[2]);
  not not_19 (not_19_out, High[0]);
  not not_20 (not_20_out, High[0]);
  not not_21 (not_21_out, High[2]);
  not not_22 (not_22_out, High[0]);
  not not_23 (not_23_out, High[2]);
  not not_24 (not_24_out, High[0]);
  not not_25 (not_25_out, High[2]);
  not not_26 (not_26_out, High[0]);
  not not_27 (not_27_out, High[1]);
  not not_28 (not_28_out, High[2]);
  not not_29 (not_29_out, High[0]);
  not not_30 (not_30_out, High[2]);
  not not_31 (not_31_out, High[0]);
  not not_32 (not_32_out, High[1]);
  or or_1 (Zero[6], not_1_out, High[1], High[2], High[3]);
  and and_1 (and_1_out, not_2_out, not_3_out);
  and and_2 (and_2_out, High[2], High[0]);
  and and_3 (and_3_out, not_4_out, not_5_out);
  and and_4 (and_4_out, High[2], not_6_out);
  and and_5 (and_5_out, High[2], not_7_out);
  not not_33 (not_33_out, High[2]);
  and and_6 (and_6_out, not_8_out, not_9_out);
  and and_7 (and_7_out, High[2], High[1], High[0]);
  not not_34 (not_34_out, High[0]);
  and and_8 (and_8_out, not_10_out, High[1]);
  and and_9 (and_9_out, High[2], not_11_out);
  and and_10 (and_10_out, not_12_out, High[1]);
  and and_11 (and_11_out, High[2], not_13_out);
  and and_12 (and_12_out, High[2], not_14_out);
  and and_13 (and_13_out, High[2], High[1], High[0]);
  and and_14 (and_14_out, not_18_out, not_19_out);
  and and_15 (and_15_out, High[1], not_20_out);
  not not_35 (not_35_out, High[1]);
  and and_16 (and_16_out, not_21_out, High[0]);
  and and_17 (and_17_out, High[2], not_22_out);
  and and_18 (and_18_out, High[0], High[1], High[2]);
  and and_19 (and_19_out, not_23_out, not_24_out);
  and and_20 (and_20_out, not_25_out, High[1]);
  and and_21 (and_21_out, High[1], not_26_out);
  and and_22 (and_22_out, High[2], not_27_out, High[0]);
  and and_23 (and_23_out, not_28_out, not_29_out);
  and and_24 (and_24_out, not_30_out, High[1]);
  and and_25 (and_25_out, High[1], not_31_out);
  and and_26 (and_26_out, High[2], not_32_out, High[0]);
  or or_2 (Zero[5], and_1_out, High[1], and_2_out, High[3]);
  or or_3 (One[6], and_3_out, and_4_out, and_5_out, High[3]);
  or or_4 (One[4], not_33_out, and_6_out, and_7_out);
  or or_5 (Two[6], not_34_out, and_8_out, and_9_out, High[3]);
  or or_6 (Two[5], and_10_out, and_11_out, and_12_out, High[3]);
  or or_7 (Two[4], not_15_out, not_16_out, not_17_out, and_13_out);
  or or_8 (Three[6], and_14_out, and_15_out);
  or or_9 (Three[4], not_35_out, and_16_out, and_17_out, and_18_out);
  or or_10 (Four[6], and_19_out, and_20_out, and_21_out, and_22_out, High[3]);
  or or_11 (Four[5], and_23_out, and_24_out, and_25_out, and_26_out, High[3]);
  not not_36 (not_36_out, Low[0]);
  not not_37 (not_37_out, Low[2]);
  and and_27 (and_27_out, not_37_out, not_38_out);
  not not_38 (not_38_out, Low[0]);
  and and_28 (and_28_out, Low[2], Low[0]);
  not not_39 (not_39_out, Low[1]);
  and and_29 (and_29_out, not_39_out, not_40_out);
  not not_40 (not_40_out, Low[0]);
  and and_30 (and_30_out, Low[2], not_41_out);
  not not_41 (not_41_out, Low[1]);
  and and_31 (and_31_out, Low[2], not_42_out);
  not not_42 (not_42_out, Low[0]);
  not not_43 (not_43_out, Low[2]);
  not not_44 (not_44_out, Low[1]);
  and and_32 (and_32_out, not_44_out, not_45_out);
  not not_45 (not_45_out, Low[0]);
  not not_46 (not_46_out, Low[0]);
  not not_47 (not_47_out, Low[2]);
  and and_33 (and_33_out, not_47_out, Low[1]);
  and and_34 (and_34_out, Low[2], not_48_out);
  not not_48 (not_48_out, Low[1]);
  not not_49 (not_49_out, Low[2]);
  and and_35 (and_35_out, not_49_out, Low[1]);
  and and_36 (and_36_out, Low[2], not_50_out);
  not not_50 (not_50_out, Low[1]);
  and and_37 (and_37_out, Low[2], not_51_out);
  not not_51 (not_51_out, Low[0]);
  not not_52 (not_52_out, Low[2]);
  not not_53 (not_53_out, Low[1]);
  not not_54 (not_54_out, Low[0]);
  and and_38 (and_38_out, Low[2], Low[1], Low[0]);
  not not_55 (not_55_out, Low[2]);
  and and_39 (and_39_out, not_55_out, not_56_out);
  not not_56 (not_56_out, Low[0]);
  and and_40 (and_40_out, Low[1], not_57_out);
  not not_57 (not_57_out, Low[0]);
  not not_58 (not_58_out, Low[1]);
  not not_59 (not_59_out, Low[2]);
  and and_41 (and_41_out, not_59_out, Low[0]);
  and and_42 (and_42_out, Low[2], not_60_out);
  not not_60 (not_60_out, Low[0]);
  and and_43 (and_43_out, Low[2], Low[1], Low[0]);
  not not_61 (not_61_out, Low[2]);
  and and_44 (and_44_out, not_61_out, not_62_out);
  not not_62 (not_62_out, Low[0]);
  not not_63 (not_63_out, Low[2]);
  and and_45 (and_45_out, not_63_out, Low[1]);
  and and_46 (and_46_out, Low[1], not_64_out);
  not not_64 (not_64_out, Low[0]);
  not not_65 (not_65_out, Low[1]);
  and and_47 (and_47_out, Low[2], not_65_out, Low[0]);
  not not_66 (not_66_out, Low[2]);
  and and_48 (and_48_out, not_66_out, not_67_out);
  not not_67 (not_67_out, Low[0]);
  not not_68 (not_68_out, Low[2]);
  and and_49 (and_49_out, not_68_out, Low[1]);
  and and_50 (and_50_out, Low[1], not_69_out);
  not not_69 (not_69_out, Low[0]);
  not not_70 (not_70_out, Low[1]);
  and and_51 (and_51_out, Low[2], not_70_out, Low[0]);
  or or_12 (Zero[2], not_36_out, Low[1], Low[2], Low[3]);
  or or_13 (Zero[1], and_27_out, Low[1], and_28_out, Low[3]);
  or or_14 (One[2], and_29_out, and_30_out, and_31_out, Low[3]);
  or or_15 (One[0], not_43_out, and_52_out, and_32_out);
  and and_52 (and_52_out, Low[2], Low[1], Low[0]);
  or or_16 (Two[2], not_46_out, and_33_out, and_34_out, Low[3]);
  or or_17 (Two[1], and_35_out, and_36_out, and_37_out, Low[3]);
  or or_18 (Two[0], not_52_out, not_53_out, not_54_out, and_38_out);
  or or_19 (Three[2], and_39_out, and_40_out);
  or or_20 (Three[0], not_58_out, and_41_out, and_42_out, and_43_out);
  or or_21 (Four[2], and_44_out, and_45_out, and_46_out, and_47_out, Low[3]);
  or or_22 (Four[1], and_48_out, and_49_out, and_50_out, and_51_out, Low[3]);
  // NOT_Gate not_71 is placed but not wired

  assign {Four[7], Four[4:3], Four[0]} = 4'b0101;
  assign {One[7], One[5], One[3], One[1]} = 4'b0000;
  assign {Three[7], Three[5], Three[3], Three[1]} = 4'b0000;
  assign {Two[7], Two[3]} = 2'b00;
  assign {Zero[7], Zero[4:3], Zero[0]} = 4'b0101;
endmodule
module MUX6x3 (
  input  [2:0] in_1,
  input  [2:0] in_2,
  input  [2:0] in_3,
  input  [2:0] in_4,
  input  [2:0] in_5,
  input  [2:0] in_6,
  input  [2:0] current_state,
  output [2:0] out_8
);

  wire helper6_1_o1, helper6_1_o2, helper6_1_o3, helper6_1_o4, helper6_1_o5, helper6_1_o6;
  wire [2:0] mask3bit_1_out_3, mask3bit_2_out_3, mask3bit_3_out_3, mask3bit_4_out_3, mask3bit_5_out_3,
       mask3bit_6_out_3;

  mask3bit mask3bit_1 (.in_1(in_1), .in_2(helper6_1_o1), .out_3(mask3bit_1_out_3));
  mask3bit mask3bit_2 (.in_1(in_2), .in_2(helper6_1_o2), .out_3(mask3bit_2_out_3));
  mask3bit mask3bit_3 (.in_1(in_3), .in_2(helper6_1_o3), .out_3(mask3bit_3_out_3));
  mask3bit mask3bit_4 (.in_1(in_4), .in_2(helper6_1_o4), .out_3(mask3bit_4_out_3));
  helper6 helper6_1 (
    .in_1(current_state), .O1(helper6_1_o1), .O2(helper6_1_o2), .O3(helper6_1_o3), .O4(helper6_1_o4),
    .O5(helper6_1_o5), .O6(helper6_1_o6));
  mask3bit mask3bit_5 (.in_1(in_5), .in_2(helper6_1_o5), .out_3(mask3bit_5_out_3));
  mask3bit mask3bit_6 (.in_1(in_6), .in_2(helper6_1_o6), .out_3(mask3bit_6_out_3));
  assign out_8 = mask3bit_1_out_3 | mask3bit_2_out_3 | mask3bit_3_out_3 | mask3bit_4_out_3 | mask3bit_5_out_3 | mask3bit_6_out_3;  // OR_Gate or_1, 3 bits wide
endmodule

module mask3bit (
  input  [2:0] in_1,
  input  in_2,
  output [2:0] out_3
);

  assign out_3 = in_1 & {3{in_2}};  // AND_Gate and_1, 3 bits wide
endmodule

module helper6 (
  input  [2:0] in_1,
  output O1,
  output O2,
  output O3,
  output O4,
  output O5,
  output O6
);

  wire and_6_out, not_1_out, not_2_out, not_3_out, not_4_out, not_5_out, not_6_out, not_7_out, not_8_out,
       not_9_out, not_10_out, or_1_out;

  not not_1 (not_1_out, in_1[2]);
  not not_2 (not_2_out, in_1[1]);
  not not_3 (not_3_out, in_1[2]);
  not not_4 (not_4_out, in_1[0]);
  not not_5 (not_5_out, in_1[2]);
  not not_6 (not_6_out, in_1[1]);
  not not_7 (not_7_out, in_1[0]);
  not not_8 (not_8_out, in_1[1]);
  not not_9 (not_9_out, in_1[0]);
  and and_1 (O1, not_1_out, not_2_out, in_1[0]);
  and and_2 (O2, not_3_out, in_1[1], not_4_out);
  and and_3 (O3, not_5_out, in_1[1], in_1[0]);
  and and_4 (O4, in_1[2], not_6_out, not_7_out);
  and and_5 (O5, in_1[2], not_8_out, in_1[0]);
  and and_6 (and_6_out, in_1[2], in_1[1], not_9_out);
  not not_10 (not_10_out, or_1_out);
  or or_1 (or_1_out, in_1[2], in_1[1], in_1[0]);
  or or_2 (O6, and_6_out, not_10_out);
endmodule
